// Logisim project AA05.circ as structural Verilog: 6 circuits, main circuit prob1
module prob1 (
  input  [7:0] input_1,
  output [7:0] output_1
);

  wire [7:0] not_1_out;

  not not_1 (not_1_out[0], input_1[0]);
  not not_2 (not_1_out[1], input_1[1]);
  not not_3 (not_1_out[2], input_1[2]);
  not not_4 (not_1_out[3], input_1[3]);
  not not_5 (not_1_out[4], input_1[4]);
  not not_6 (not_1_out[5], input_1[5]);
  not not_7 (not_1_out[6], input_1[6]);
  not not_8 (not_1_out[7], input_1[7]);
  full_adder_8_bit full_adder_8_bit_1 (.a(not_1_out), .b(8'h1), .s(output_1));  // open: cout
endmodule

module prob2 (
  input  [7:0] input_2,
  output [7:0] output_2
);

  wire [7:0] prob1_1_output_1;

  prob1 prob1_1 (.input_1(input_2), .output_1(prob1_1_output_1));
  mux_2_1 mux_2_1_1 (.a(input_2[0]), .b(prob1_1_output_1[0]), .x(input_2[7]), .o(output_2[0]));
  mux_2_1 mux_2_1_2 (.a(input_2[1]), .b(prob1_1_output_1[1]), .x(input_2[7]), .o(output_2[1]));
  mux_2_1 mux_2_1_3 (.a(input_2[2]), .b(prob1_1_output_1[2]), .x(input_2[7]), .o(output_2[2]));
  mux_2_1 mux_2_1_4 (.a(input_2[3]), .b(prob1_1_output_1[3]), .x(input_2[7]), .o(output_2[3]));
  mux_2_1 mux_2_1_5 (.a(input_2[4]), .b(prob1_1_output_1[4]), .x(input_2[7]), .o(output_2[4]));
  mux_2_1 mux_2_1_6 (.a(input_2[5]), .b(prob1_1_output_1[5]), .x(input_2[7]), .o(output_2[5]));
  mux_2_1 mux_2_1_7 (.a(input_2[6]), .b(prob1_1_output_1[6]), .x(input_2[7]), .o(output_2[6]));
  mux_2_1 mux_2_1_8 (.a(input_2[7]), .b(prob1_1_output_1[7]), .x(input_2[7]), .o(output_2[7]));
endmodule

module full_adder (
  input  a,
  input  b,
  input  cin,
  output s,
  output cout
);

  wire and_1_out, and_2_out, xor_1_out;

  xor xor_1 (xor_1_out, a, b);
  xor xor_2 (s, xor_1_out, cin);
  and and_1 (and_1_out, xor_1_out, cin);
  and and_2 (and_2_out, a, b);
  or or_1 (cout, and_1_out, and_2_out);
endmodule

module full_adder_8_bit (
  input  [7:0] a,
  input  [7:0] b,
  output [7:0] s,
  output cout
);

  wire full_adder_1_cout, full_adder_2_cout, full_adder_3_cout, full_adder_4_cout, full_adder_5_cout,
       full_adder_6_cout, full_adder_7_cout;

  full_adder full_adder_1 (.a(a[0]), .b(b[0]), .s(s[0]), .cout(full_adder_1_cout));  // open: cin
  full_adder full_adder_2 (.a(a[1]), .b(b[1]), .cin(full_adder_1_cout), .s(s[1]), .cout(full_adder_2_cout));
  full_adder full_adder_3 (.a(a[2]), .b(b[2]), .cin(full_adder_2_cout), .s(s[2]), .cout(full_adder_3_cout));
  full_adder full_adder_4 (.a(a[3]), .b(b[3]), .cin(full_adder_3_cout), .s(s[3]), .cout(full_adder_4_cout));
  full_adder full_adder_5 (.a(a[4]), .b(b[4]), .cin(full_adder_4_cout), .s(s[4]), .cout(full_adder_5_cout));
  full_adder full_adder_6 (.a(a[5]), .b(b[5]), .cin(full_adder_5_cout), .s(s[5]), .cout(full_adder_6_cout));
  full_adder full_adder_7 (.a(a[6]), .b(b[6]), .cin(full_adder_6_cout), .s(s[6]), .cout(full_adder_7_cout));
  full_adder full_adder_8 (.a(a[7]), .b(b[7]), .cin(full_adder_7_cout), .s(s[7]), .cout(cout));
endmodule

module mux_2_1 (
  input  a,
  input  b,
  input  x,
  output o
);

  wire and_1_out, and_2_out, not_1_out;

  not not_1 (not_1_out, x);
  and and_1 (and_1_out, a, not_1_out);
  and and_2 (and_2_out, b, x);
  or or_1 (o, and_1_out, and_2_out);
endmodule

module prob3 (
  input  [15:0] a,
  input  [15:0] b,
  input  [15:0] c,
  output [15:0] out_4
);

  wire comparator_1_lt, comparator_2_lt;
  wire [15:0] multiplexer_1_out;

  Comparator #(.width(16)) comparator_1 (.a(a), .b(b), .lt(comparator_1_lt));  // open: gt, eq
  Multiplexer #(.width(16)) multiplexer_1 (.in0(a), .in1(b), .out(multiplexer_1_out), .sel(comparator_1_lt));
  Comparator #(.width(16)) comparator_2 (.a(multiplexer_1_out), .b(c), .lt(comparator_2_lt));  // open: gt, eq
  Multiplexer #(.width(16)) multiplexer_2 (.in0(multiplexer_1_out), .in1(c), .out(out_4), .sel(comparator_2_lt));
endmodule
