// Logisim project project2.circ as structural Verilog: 4 circuits, main circuit regfile
module CPU (
  input  [31:0] instruction
);

  wire clock_1_out, control_1_immsel, control_1_reg_write_e, control_1_shiftsel, control_1_w_e_mem;
  wire [3:0] control_1_alusel;
  wire [4:0] control_1_rd, control_1_rs, control_1_rt, multiplexer_1_out;
  wire [15:0] bit_extender_1_out;
  wire [31:0] alu_1_res, control_1_imm, control_1_shamt, multiplexer_2_out, multiplexer_3_out,
       multiplexer_4_out, regfile_1_rs_data, regfile_1_rt_data, shifter_1_out;

  Multiplexer #(.width(5)) multiplexer_1 (
    .in0(control_1_rd), .in1(control_1_rt), .out(multiplexer_1_out), .sel(control_1_immsel));
  regfile regfile_1 (
    .rd_data(alu_1_res), .write_e(control_1_reg_write_e), .rd(multiplexer_1_out), .rt(control_1_rt),
    .rs(control_1_rs), .rs_data(regfile_1_rs_data), .rt_data(regfile_1_rt_data));
  Multiplexer #(.width(32)) multiplexer_2 (
    .in0(regfile_1_rs_data), .in1(regfile_1_rt_data), .out(multiplexer_2_out), .sel(control_1_shiftsel));
  Control control_1 (
    .inst(instruction), .shamt(control_1_shamt), .rd(control_1_rd), .imm(control_1_imm),
    .immSel(control_1_immsel), .rt(control_1_rt), .rs(control_1_rs), .reg_write_e(control_1_reg_write_e),
    .shiftSel(control_1_shiftsel), .ALUSel(control_1_alusel), .w_e_mem(control_1_w_e_mem));
  Multiplexer #(.width(32)) multiplexer_3 (
    .in0(regfile_1_rt_data), .in1(control_1_imm), .out(multiplexer_3_out), .sel(control_1_immsel));
  Multiplexer #(.width(32)) multiplexer_4 (
    .in0(multiplexer_3_out), .in1(control_1_shamt), .out(multiplexer_4_out), .sel(control_1_shiftsel));
  ALU alu_1 (.OP2(multiplexer_4_out), .ALUCode(control_1_alusel), .OP1(multiplexer_2_out), .Res(alu_1_res));
  Bit_Extender #(.in_width(32)) bit_extender_1 (.in(shifter_1_out), .out(bit_extender_1_out));
  Shifter #(.shift("lr"), .width(32)) shifter_1 (.in(alu_1_res), .\dist (5'b11110), .out(shifter_1_out));
  RAM #(.addrWidth(16), .dataWidth(32), .enables("line")) ram_1 (
    .addr(bit_extender_1_out), .we(control_1_w_e_mem), .clk(clock_1_out));  // open: din, dout
  Clock clock_1 (.out(clock_1_out));

  // Notes on the sheet:
  //   shiftSel
  //   immSel
  //   shiftSel
endmodule

module regfile (
  input  [31:0] rd_data,
  input  [4:0] rd,
  input  write_e,
  input  [4:0] rs,
  input  [4:0] rt,
  output [31:0] rs_data,
  output [31:0] rt_data
);

  wire and_1_out, clock_1_out, demultiplexer_1_out0, demultiplexer_1_out1, demultiplexer_1_out2,
       demultiplexer_1_out3, demultiplexer_1_out4, demultiplexer_1_out5, demultiplexer_1_out6,
       demultiplexer_1_out7, demultiplexer_1_out8, demultiplexer_1_out9, demultiplexer_1_out10,
       demultiplexer_1_out11, demultiplexer_1_out12, demultiplexer_1_out13, demultiplexer_1_out14,
       demultiplexer_1_out15, demultiplexer_1_out16, demultiplexer_1_out17, demultiplexer_1_out18,
       demultiplexer_1_out19, demultiplexer_1_out20, demultiplexer_1_out21, demultiplexer_1_out22,
       demultiplexer_1_out23, demultiplexer_1_out24, demultiplexer_1_out25, demultiplexer_1_out26,
       demultiplexer_1_out27, demultiplexer_1_out28, demultiplexer_1_out29, demultiplexer_1_out30,
       demultiplexer_1_out31;
  wire [31:0] R0_q, R1_q, R2_q, R3_q, R4_q, R5_q, R6_q, R7_q, R8_q, R9_q, R10_q, R11_q, R12_q, R13_q, R14_q,
       R15_q, R16_q, R17_q, R18_q, R19_q, R20_q, R21_q, R22_q, R23_q, R24_q, R25_q, R26_q, R27_q, R28_q,
       R29_q, R30_q, R31_q;

  Clock clock_1 (.out(clock_1_out));
  Demultiplexer #(.select(5)) demultiplexer_1 (
    .out0(demultiplexer_1_out0), .out1(demultiplexer_1_out1), .out2(demultiplexer_1_out2),
    .out3(demultiplexer_1_out3), .out4(demultiplexer_1_out4), .out5(demultiplexer_1_out5),
    .out6(demultiplexer_1_out6), .out7(demultiplexer_1_out7), .out8(demultiplexer_1_out8),
    .out9(demultiplexer_1_out9), .out10(demultiplexer_1_out10), .out11(demultiplexer_1_out11),
    .out12(demultiplexer_1_out12), .out13(demultiplexer_1_out13), .out14(demultiplexer_1_out14),
    .out15(demultiplexer_1_out15), .out16(demultiplexer_1_out16), .out17(demultiplexer_1_out17),
    .out18(demultiplexer_1_out18), .out19(demultiplexer_1_out19), .out20(demultiplexer_1_out20),
    .out21(demultiplexer_1_out21), .out22(demultiplexer_1_out22), .out23(demultiplexer_1_out23),
    .out24(demultiplexer_1_out24), .out25(demultiplexer_1_out25), .out26(demultiplexer_1_out26),
    .out27(demultiplexer_1_out27), .out28(demultiplexer_1_out28), .out29(demultiplexer_1_out29),
    .out30(demultiplexer_1_out30), .out31(demultiplexer_1_out31), .in(write_e), .sel(rd));
  Register #(.width(32)) R1 (.D(rd_data), .en(demultiplexer_1_out1), .clk(clock_1_out), .Q(R1_q));  // open: clr
  Register #(.width(32)) R2 (.D(rd_data), .en(demultiplexer_1_out2), .clk(clock_1_out), .Q(R2_q));  // open: clr
  Register #(.width(32)) R3 (.D(rd_data), .en(demultiplexer_1_out3), .clk(clock_1_out), .Q(R3_q));  // open: clr
  Register #(.width(32)) R4 (.D(rd_data), .en(demultiplexer_1_out4), .clk(clock_1_out), .Q(R4_q));  // open: clr
  Register #(.width(32)) R5 (.D(rd_data), .en(demultiplexer_1_out5), .clk(clock_1_out), .Q(R5_q));  // open: clr
  Register #(.width(32)) R6 (.D(rd_data), .en(demultiplexer_1_out6), .clk(clock_1_out), .Q(R6_q));  // open: clr
  Register #(.width(32)) R7 (.D(rd_data), .en(demultiplexer_1_out7), .clk(clock_1_out), .Q(R7_q));  // open: clr
  Register #(.width(32)) R8 (.D(rd_data), .en(demultiplexer_1_out8), .clk(clock_1_out), .Q(R8_q));  // open: clr
  Register #(.width(32)) R9 (.D(rd_data), .en(demultiplexer_1_out9), .clk(clock_1_out), .Q(R9_q));  // open: clr
  Register #(.width(32)) R10 (.D(rd_data), .en(demultiplexer_1_out10), .clk(clock_1_out), .Q(R10_q));  // open: clr
  Register #(.width(32)) R11 (.D(rd_data), .en(demultiplexer_1_out11), .clk(clock_1_out), .Q(R11_q));  // open: clr
  Register #(.width(32)) R12 (.D(rd_data), .en(demultiplexer_1_out12), .clk(clock_1_out), .Q(R12_q));  // open: clr
  Register #(.width(32)) R13 (.D(rd_data), .en(demultiplexer_1_out13), .clk(clock_1_out), .Q(R13_q));  // open: clr
  Register #(.width(32)) R14 (.D(rd_data), .en(demultiplexer_1_out14), .clk(clock_1_out), .Q(R14_q));  // open: clr
  Register #(.width(32)) R15 (.D(rd_data), .en(demultiplexer_1_out15), .clk(clock_1_out), .Q(R15_q));  // open: clr
  Register #(.width(32)) R16 (.D(rd_data), .en(demultiplexer_1_out16), .clk(clock_1_out), .Q(R16_q));  // open: clr
  Register #(.width(32)) R17 (.D(rd_data), .en(demultiplexer_1_out17), .clk(clock_1_out), .Q(R17_q));  // open: clr
  Register #(.width(32)) R18 (.D(rd_data), .en(demultiplexer_1_out18), .clk(clock_1_out), .Q(R18_q));  // open: clr
  Register #(.width(32)) R19 (.D(rd_data), .en(demultiplexer_1_out19), .clk(clock_1_out), .Q(R19_q));  // open: clr
  Register #(.width(32)) R20 (.D(rd_data), .en(demultiplexer_1_out20), .clk(clock_1_out), .Q(R20_q));  // open: clr
  Register #(.width(32)) R21 (.D(rd_data), .en(demultiplexer_1_out21), .clk(clock_1_out), .Q(R21_q));  // open: clr
  Register #(.width(32)) R22 (.D(rd_data), .en(demultiplexer_1_out22), .clk(clock_1_out), .Q(R22_q));  // open: clr
  Register #(.width(32)) R23 (.D(rd_data), .en(demultiplexer_1_out23), .clk(clock_1_out), .Q(R23_q));  // open: clr
  Register #(.width(32)) R24 (.D(rd_data), .en(demultiplexer_1_out24), .clk(clock_1_out), .Q(R24_q));  // open: clr
  Register #(.width(32)) R25 (.D(rd_data), .en(demultiplexer_1_out25), .clk(clock_1_out), .Q(R25_q));  // open: clr
  Register #(.width(32)) R26 (.D(rd_data), .en(demultiplexer_1_out26), .clk(clock_1_out), .Q(R26_q));  // open: clr
  Register #(.width(32)) R27 (.D(rd_data), .en(demultiplexer_1_out27), .clk(clock_1_out), .Q(R27_q));  // open: clr
  Register #(.width(32)) R28 (.D(rd_data), .en(demultiplexer_1_out28), .clk(clock_1_out), .Q(R28_q));  // open: clr
  Register #(.width(32)) R29 (.D(rd_data), .en(demultiplexer_1_out29), .clk(clock_1_out), .Q(R29_q));  // open: clr
  Register #(.width(32)) R30 (.D(rd_data), .en(demultiplexer_1_out30), .clk(clock_1_out), .Q(R30_q));  // open: clr
  and and_1 (and_1_out, demultiplexer_1_out0, 1'b0);
  Register #(.width(32)) R31 (.D(rd_data), .en(demultiplexer_1_out31), .clk(clock_1_out), .Q(R31_q));  // open: clr
  Register #(.width(32)) R0 (.D(rd_data), .en(and_1_out), .clk(clock_1_out), .Q(R0_q));  // open: clr
  Multiplexer #(.select(5), .width(32)) multiplexer_1 (
    .in0(R0_q), .in1(R1_q), .in2(R2_q), .in3(R3_q), .in4(R4_q), .in5(R5_q), .in6(R6_q), .in7(R7_q),
    .in8(R8_q), .in9(R9_q), .in10(R10_q), .in11(R11_q), .in12(R12_q), .in13(R13_q), .in14(R14_q),
    .in15(R15_q), .in16(R16_q), .in17(R17_q), .in18(R18_q), .in19(R19_q), .in20(R20_q), .in21(R21_q),
    .in22(R22_q), .in23(R23_q), .in24(R24_q), .in25(R25_q), .in26(R26_q), .in27(R27_q), .in28(R28_q),
    .in29(R29_q), .in30(R30_q), .in31(R31_q), .out(rs_data), .sel(rs));
  Multiplexer #(.select(5), .width(32)) multiplexer_2 (
    .in0(R0_q), .in1(R1_q), .in2(R2_q), .in3(R3_q), .in4(R4_q), .in5(R5_q), .in6(R6_q), .in7(R7_q),
    .in8(R8_q), .in9(R9_q), .in10(R10_q), .in11(R11_q), .in12(R12_q), .in13(R13_q), .in14(R14_q),
    .in15(R15_q), .in16(R16_q), .in17(R17_q), .in18(R18_q), .in19(R19_q), .in20(R20_q), .in21(R21_q),
    .in22(R22_q), .in23(R23_q), .in24(R24_q), .in25(R25_q), .in26(R26_q), .in27(R27_q), .in28(R28_q),
    .in29(R29_q), .in30(R30_q), .in31(R31_q), .out(rt_data), .sel(rt));
endmodule

module ALU (
  input  [3:0] ALUCode,
  input  [31:0] OP1,
  input  [31:0] OP2,
  output [31:0] Res
);

  wire clock_1_out, clock_2_out, comparator_1_lt, comparator_2_eq, comparator_3_eq, or_1_out;
  wire [4:0] bit_extender_1_out, bit_extender_2_out;
  wire [31:0] adder_1_out, bit_extender_3_out, bit_extender_4_out, bit_extender_5_out, divider_1_out,
       divider_1_rem, HI_q, LO_q, multiplexer_2_out, multiplexer_3_out, multiplier_1_out, shifter_1_out,
       shifter_2_out, subtractor_1_out;

  Bit_Extender #(.in_width(32), .out_width(5)) bit_extender_1 (.in(OP2), .out(bit_extender_1_out));
  Bit_Extender #(.in_width(32), .out_width(5)) bit_extender_2 (.in(OP2), .out(bit_extender_2_out));
  Adder #(.width(32)) adder_1 (.a(OP1), .b(OP2), .out(adder_1_out));  // open: cin, cout
  Subtractor #(.width(32)) subtractor_1 (.a(OP1), .b(OP2), .out(subtractor_1_out));  // open: bin, bout
  Multiplier #(.width(32)) multiplier_1 (.a(OP1), .b(OP2), .out(multiplier_1_out));  // open: cin, cout
  Divider #(.width(32)) divider_1 (.a(OP1), .b(OP2), .out(divider_1_out), .rem(divider_1_rem));  // open: upper
  Shifter #(.width(32)) shifter_1 (.in(OP1), .\dist (bit_extender_1_out), .out(shifter_1_out));
  Shifter #(.shift("lr"), .width(32)) shifter_2 (.in(OP1), .\dist (bit_extender_2_out), .out(shifter_2_out));
  Comparator #(.mode("unsigned"), .width(32)) comparator_1 (.a(OP1), .b(OP2), .lt(comparator_1_lt));  // open: gt, eq
  assign bit_extender_3_out = {{31{1'b0}}, comparator_1_lt};  // Bit_Extender bit_extender_3
  Multiplexer #(.select(4), .width(32)) multiplexer_1 (
    .in0(adder_1_out), .in1(subtractor_1_out), .in4(shifter_1_out), .in5(shifter_2_out),
    .in6(bit_extender_3_out), .in7(HI_q), .in8(LO_q), .out(Res), .sel(ALUCode));  // open: in2, in3, in9, in10, in11, in12, in13, in14, in15
  assign bit_extender_4_out = {{16{multiplier_1_out[31]}}, multiplier_1_out[31:16]};  // Bit_Extender bit_extender_4
  assign bit_extender_5_out = {{16{multiplier_1_out[15]}}, multiplier_1_out[15:0]};  // Bit_Extender bit_extender_5
  Comparator #(.mode("unsigned"), .width(4)) comparator_2 (
    .a(4'b0010), .b(ALUCode), .eq(comparator_2_eq));  // open: gt, lt
  Comparator #(.mode("unsigned"), .width(4)) comparator_3 (
    .a(4'b0011), .b(ALUCode), .eq(comparator_3_eq));  // open: gt, lt
  Multiplexer #(.width(32)) multiplexer_2 (
    .in0(bit_extender_4_out), .in1(divider_1_rem), .out(multiplexer_2_out), .sel(comparator_3_eq));
  Multiplexer #(.width(32)) multiplexer_3 (
    .in0(bit_extender_5_out), .in1(divider_1_out), .out(multiplexer_3_out), .sel(comparator_3_eq));
  or or_1 (or_1_out, comparator_2_eq, comparator_3_eq);
  Register #(.width(32)) HI (.D(multiplexer_2_out), .en(or_1_out), .clk(clock_1_out), .Q(HI_q));  // open: clr
  Clock clock_1 (.out(clock_1_out));
  Register #(.width(32)) LO (.D(multiplexer_3_out), .en(or_1_out), .clk(clock_2_out), .Q(LO_q));  // open: clr
  Clock clock_2 (.out(clock_2_out));

  // Notes on the sheet:
  //   add & addi
  //   sub
  //   slt
  //   mult
  //   div
  //   sll
  //   srl
  //   mult
  //   div
endmodule

module Control (
  input  [31:0] inst,
  output [31:0] shamt,
  output [4:0] rd,
  output [31:0] imm,
  output immSel,
  output [4:0] rt,
  output [4:0] rs,
  output reg_write_e,
  output shiftSel,
  output [3:0] ALUSel,
  output w_e_mem
);

  wire comparator_1_eq, comparator_3_eq, comparator_4_eq, comparator_5_eq, comparator_6_eq, comparator_7_eq,
       comparator_8_eq, comparator_9_eq, comparator_10_eq, comparator_11_eq, or_1_out, or_2_out;
  wire [5:0] multiplexer_1_out;
  wire [10:0] demultiplexer_1_out0;
  wire [15:0] demultiplexer_1_out1;

  Comparator #(.width(6)) comparator_1 (.a(inst[31:26]), .b({6{1'b0}}), .eq(comparator_1_eq));  // open: gt, lt
  Comparator #(.width(6)) comparator_2 (.a(inst[31:26]), .b(6'b001000), .eq(immSel));  // open: gt, lt
  Demultiplexer #(.width(16)) demultiplexer_1 (
    .out0({rd, demultiplexer_1_out0}), .out1(demultiplexer_1_out1), .in(inst[15:0]), .sel(immSel));
  Multiplexer #(.width(6)) multiplexer_1 (
    .in0({6{1'b1}}), .in1(inst[5:0]), .out(multiplexer_1_out), .sel(comparator_1_eq));
  Comparator #(.width(6)) comparator_3 (.a(multiplexer_1_out), .b(6'b100000), .eq(comparator_3_eq));  // open: gt, lt
  Comparator #(.width(6)) comparator_4 (.a(multiplexer_1_out), .b(6'b100010), .eq(comparator_4_eq));  // open: gt, lt
  Comparator #(.width(6)) comparator_5 (.a(multiplexer_1_out), .b(6'b011000), .eq(comparator_5_eq));  // open: gt, lt
  Comparator #(.width(6)) comparator_6 (.a(multiplexer_1_out), .b(6'b011010), .eq(comparator_6_eq));  // open: gt, lt
  Comparator #(.width(6)) comparator_7 (.a(multiplexer_1_out), .b(6'b010010), .eq(comparator_7_eq));  // open: gt, lt
  Comparator #(.width(6)) comparator_8 (.a(multiplexer_1_out), .b(6'b010000), .eq(comparator_8_eq));  // open: gt, lt
  Comparator #(.width(6)) comparator_9 (.a(multiplexer_1_out), .b({6{1'b0}}), .eq(comparator_9_eq));  // open: gt, lt
  Comparator #(.width(6)) comparator_10 (.a(multiplexer_1_out), .b(6'b000010), .eq(comparator_10_eq));  // open: gt, lt
  Comparator #(.width(6)) comparator_11 (.a(multiplexer_1_out), .b(6'b101010), .eq(comparator_11_eq));  // open: gt, lt
  or or_1 (or_1_out, immSel, comparator_3_eq);
  Multiplexer #(.width(4)) multiplexer_2 (.in1(4'b0000), .out(ALUSel), .sel(or_1_out));  // open: in0
  Multiplexer #(.width(4)) multiplexer_3 (.in1(4'b0001), .out(ALUSel), .sel(comparator_4_eq));  // open: in0
  Multiplexer #(.width(4)) multiplexer_4 (.in1(4'b0010), .out(ALUSel), .sel(comparator_5_eq));  // open: in0
  Multiplexer #(.width(4)) multiplexer_5 (.in1(4'b0011), .out(ALUSel), .sel(comparator_6_eq));  // open: in0
  Multiplexer #(.width(4)) multiplexer_6 (.in1(4'b1000), .out(ALUSel), .sel(comparator_7_eq));  // open: in0
  Multiplexer #(.width(4)) multiplexer_7 (.in1(4'b0111), .out(ALUSel), .sel(comparator_8_eq));  // open: in0
  Multiplexer #(.width(4)) multiplexer_8 (.in1(4'b0100), .out(ALUSel), .sel(comparator_9_eq));  // open: in0
  Multiplexer #(.width(4)) multiplexer_9 (.in1(4'b0101), .out(ALUSel), .sel(comparator_10_eq));  // open: in0
  Multiplexer #(.width(4)) multiplexer_10 (.in1(4'b0110), .out(ALUSel), .sel(comparator_11_eq));  // open: in0
  assign shamt = {{27{demultiplexer_1_out0[10]}}, demultiplexer_1_out0[10:6]};  // Bit_Extender bit_extender_1
  assign imm = {{16{demultiplexer_1_out1[15]}}, demultiplexer_1_out1};  // Bit_Extender bit_extender_2
  or or_2 (or_2_out, comparator_5_eq, comparator_6_eq);
  not not_1 (reg_write_e, or_2_out);
  or or_3 (shiftSel, comparator_9_eq, comparator_10_eq);

  assign rs = inst[25:21];
  assign rt = inst[20:16];

  // Notes on the sheet:
  //   funct
  //   op 001000
  //   op 000000
  //   add
  //   sub
  //   mult
  //   div
  //   mflo
  //   mfhi
  //   sll
  //   srl
  //   slt
endmodule
