// Logisim project project3.circ as structural Verilog: 4 circuits, main circuit regfile
module CPU (
);

  wire alu_1_equal, and_1_out, and_2_out, clock_1_out, clock_2_out, control_1_beqselect, control_1_bneselect,
       control_1_immselect, control_1_jalr, control_1_jalselect, control_1_jrselect, control_1_jselect,
       control_1_lwselect, control_1_reg_write_e, control_1_shiftslect, control_1_swselect, or_1_out,
       or_2_out, or_3_out, or_4_out;
  wire [3:0] control_1_alu_select;
  wire [4:0] control_1_rd, control_1_rs, control_1_rt;
  wire [15:0] bit_extender_2_out, bit_extender_4_out;
  wire [25:0] bit_extender_3_out, shifter_2_out;
  wire [31:0] adder_1_out, adder_2_out, adder_3_out, alu_1_out_4, bit_extender_1_out, control_1_imm,
       control_1_sa, multiplexer_1_out, multiplexer_2_out, multiplexer_3_out, multiplexer_4_out,
       multiplexer_5_out, multiplexer_6_out, multiplexer_7_out, ProgramCounter_q, ram_1_dout,
       regfile_1_rs_data, regfile_1_rt_data, rom_1_data, shifter_1_out, shifter_3_out, shifter_4_out;

  Adder #(.width(32)) adder_1 (.a(ProgramCounter_q), .b(32'h4), .out(adder_1_out));  // open: cin, cout
  Shifter #(.width(32)) shifter_1 (.in(control_1_imm), .\dist (5'b00010), .out(shifter_1_out));
  Adder #(.width(32)) adder_2 (.a(adder_1_out), .b(shifter_1_out), .out(adder_2_out));  // open: cin, cout
  Shifter #(.width(26)) shifter_2 (.in(bit_extender_3_out), .\dist (5'b00010), .out(shifter_2_out));
  Multiplexer #(.width(32)) multiplexer_1 (
    .in0(adder_1_out), .in1(adder_2_out), .out(multiplexer_1_out), .sel(or_4_out));
  assign bit_extender_1_out = {{6{shifter_2_out[25]}}, shifter_2_out};  // Bit_Extender bit_extender_1
  Multiplexer #(.width(32)) multiplexer_2 (
    .in0(multiplexer_1_out), .in1(multiplexer_3_out), .out(multiplexer_2_out), .sel(or_1_out));
  Multiplexer #(.width(32)) multiplexer_3 (
    .in0(bit_extender_1_out), .in1(adder_3_out), .out(multiplexer_3_out), .sel(or_2_out));
  Adder #(.width(32)) adder_3 (.a(regfile_1_rs_data), .b(32'h2), .out(adder_3_out));  // open: cin, cout
  or or_1 (or_1_out, or_2_out, control_1_jselect, or_3_out);
  Register #(.width(32)) ProgramCounter (
    .D(multiplexer_2_out), .en(1'b1), .clk(clock_1_out), .Q(ProgramCounter_q));  // open: clr
  Clock clock_1 (.out(clock_1_out));
  Shifter #(.shift("lr"), .width(32)) shifter_3 (.in(ProgramCounter_q), .\dist (5'b00010), .out(shifter_3_out));
  ROM #(.addrWidth(16), .dataWidth(32)) rom_1 (.addr(bit_extender_2_out), .data(rom_1_data));
  Bit_Extender #(.in_width(32)) bit_extender_2 (.in(shifter_3_out), .out(bit_extender_2_out));
  Bit_Extender #(.in_width(32), .out_width(26)) bit_extender_3 (.in(rom_1_data), .out(bit_extender_3_out));
  Multiplexer #(.width(32)) multiplexer_4 (
    .in0(alu_1_out_4), .in1(ram_1_dout), .out(multiplexer_4_out), .sel(control_1_lwselect));
  or or_2 (or_2_out, control_1_jrselect, control_1_jalr);
  or or_3 (or_3_out, control_1_jalr, control_1_jalselect);
  Multiplexer #(.width(32)) multiplexer_5 (
    .in0(multiplexer_4_out), .in1(adder_1_out), .out(multiplexer_5_out), .sel(or_3_out));
  or or_4 (or_4_out, and_1_out, and_2_out);
  Control control_1 (
    .Inst(rom_1_data), .lwSelect(control_1_lwselect), .swSelect(control_1_swselect),
    .beqSelect(control_1_beqselect), .bneSelect(control_1_bneselect), .jSelect(control_1_jselect),
    .jalSelect(control_1_jalselect), .immSelect(control_1_immselect), .SA(control_1_sa), .imm(control_1_imm),
    .rs(control_1_rs), .rt(control_1_rt), .rd(control_1_rd), .reg_write_e(control_1_reg_write_e),
    .shiftSlect(control_1_shiftslect), .ALU_Select(control_1_alu_select), .jrSelect(control_1_jrselect),
    .jalr(control_1_jalr));
  regfile regfile_1 (
    .rd(control_1_rd), .rs(control_1_rs), .write(control_1_reg_write_e), .rt(control_1_rt),
    .rd_data(multiplexer_5_out), .rs_data(regfile_1_rs_data), .rt_data(regfile_1_rt_data));
  and and_1 (and_1_out, alu_1_equal, control_1_bneselect);
  and and_2 (and_2_out, alu_1_equal, control_1_beqselect);
  Multiplexer #(.width(32)) multiplexer_6 (
    .in0(regfile_1_rs_data), .in1(control_1_sa), .out(multiplexer_6_out), .sel(control_1_shiftslect));
  Multiplexer #(.width(32)) multiplexer_7 (
    .in0(regfile_1_rt_data), .in1(control_1_imm), .out(multiplexer_7_out), .sel(control_1_immselect));
  ALU alu_1 (
    .OP1(multiplexer_6_out), .OP2(multiplexer_7_out), .out_4(alu_1_out_4), .Equal(alu_1_equal));  // open: Control
  Shifter #(.shift("lr"), .width(32)) shifter_4 (.in(alu_1_out_4), .\dist (5'b11110), .out(shifter_4_out));
  Bit_Extender #(.in_width(32)) bit_extender_4 (.in(shifter_4_out), .out(bit_extender_4_out));
  Clock clock_2 (.out(clock_2_out));
  RAM #(.addrWidth(16), .dataWidth(32), .enables("line")) ram_1 (
    .addr(bit_extender_4_out), .we(control_1_swselect), .clk(clock_2_out), .dout(ram_1_dout));  // open: din

  // Notes on the sheet:
  //   PC + 4
  //   jr/jalr
  //   1 if two registers are ==
  //   imm
  //   label to jump to
  //   contents of rom_1 (hex, n*v repeats v):
  //   2008000a 20090062 95140 9c0c2 1290018 5812 148001a b010 128902a 22d3fffd 2002000a d00c
  //   rs-data
  //   ALU
  //   MEM
  //   PC + 4
  //   jal/jalr
endmodule

module regfile (
  input  write,
  input  [4:0] rd,
  input  [4:0] rt,
  input  [4:0] rs,
  input  [31:0] rd_data,
  output [31:0] rt_data,
  output [31:0] rs_data
);

  wire clock_1_out, clock_2_out, clock_3_out, clock_4_out, clock_5_out, clock_6_out, clock_7_out,
       clock_8_out, clock_9_out, clock_10_out, clock_11_out, clock_12_out, clock_13_out, clock_14_out,
       clock_15_out, clock_16_out, clock_17_out, clock_18_out, clock_19_out, clock_20_out, clock_21_out,
       clock_22_out, clock_23_out, clock_24_out, clock_25_out, clock_26_out, clock_27_out, clock_28_out,
       clock_29_out, clock_30_out, clock_31_out, clock_32_out, demultiplexer_1_out0, demultiplexer_1_out1,
       demultiplexer_1_out2, demultiplexer_1_out3, demultiplexer_1_out4, demultiplexer_1_out5,
       demultiplexer_1_out6, demultiplexer_1_out7, demultiplexer_1_out8, demultiplexer_1_out9,
       demultiplexer_1_out10, demultiplexer_1_out11, demultiplexer_1_out12, demultiplexer_1_out13,
       demultiplexer_1_out14, demultiplexer_1_out15, demultiplexer_1_out16, demultiplexer_1_out17,
       demultiplexer_1_out18, demultiplexer_1_out19, demultiplexer_1_out20, demultiplexer_1_out21,
       demultiplexer_1_out22, demultiplexer_1_out23, demultiplexer_1_out24, demultiplexer_1_out25,
       demultiplexer_1_out26, demultiplexer_1_out27, demultiplexer_1_out28, demultiplexer_1_out29,
       demultiplexer_1_out30, demultiplexer_1_out31;
  wire [31:0] a0_q, a1_q, a2_q, a3_q, at_q, gp_q, k0_q, k1_q, R0_q, ra_q, s0_q, s1_q, s2_q, s3_q, s4_q, s5_q,
       s6_q, s7_q, s8_q, sp_q, t0_q, t1_q, t2_q, t3_q, t4_q, t5_q, t6_q, t7_q, t8_q, t9_q, v0_q, v1_q;

  Multiplexer #(.select(5), .width(32)) multiplexer_1 (
    .in0(R0_q), .in2(at_q), .in3(v0_q), .in4(v1_q), .in5(a0_q), .in6(a1_q), .in7(a2_q), .in8(a3_q),
    .in9(t0_q), .in10(t1_q), .in11(t2_q), .in12(t3_q), .in13(t4_q), .in14(t5_q), .in15(t6_q), .in16(t7_q),
    .in17(s0_q), .in18(s1_q), .in19(s2_q), .in20(s3_q), .in21(s4_q), .in22(s5_q), .in23(s6_q), .in24(s7_q),
    .in25(t8_q), .in26(t9_q), .in27(k0_q), .in28(k1_q), .in29(gp_q), .in30(sp_q), .in31(s8_q), .out(rs_data),
    .sel(rs));  // open: in1
  Multiplexer #(.select(5), .width(32)) multiplexer_2 (
    .in0(R0_q), .in1(at_q), .in2(v0_q), .in3(v1_q), .in4(a0_q), .in5(a1_q), .in6(a2_q), .in7(a3_q),
    .in8(t0_q), .in9(t1_q), .in10(t2_q), .in11(t3_q), .in12(t4_q), .in13(t5_q), .in14(t6_q), .in15(t7_q),
    .in16(s0_q), .in17(s1_q), .in18(s2_q), .in19(s3_q), .in20(s4_q), .in21(s5_q), .in22(s6_q), .in23(s7_q),
    .in24(t8_q), .in25(t9_q), .in26(k0_q), .in27(k1_q), .in28(gp_q), .in29(sp_q), .in30(s8_q), .in31(ra_q),
    .out(rt_data), .sel(rt));
  Clock clock_1 (.out(clock_1_out));
  Register #(.width(32)) R0 (.D({32{1'b0}}), .en(demultiplexer_1_out0), .clk(clock_2_out), .Q(R0_q));  // open: clr
  Clock clock_2 (.out(clock_2_out));
  Register #(.width(32)) s0 (.D(rd_data), .en(demultiplexer_1_out16), .clk(clock_1_out), .Q(s0_q));  // open: clr
  Register #(.width(32)) at (.D(rd_data), .en(demultiplexer_1_out1), .clk(clock_3_out), .Q(at_q));  // open: clr
  Clock clock_3 (.out(clock_3_out));
  Register #(.width(32)) s1 (.D(rd_data), .en(demultiplexer_1_out17), .clk(clock_4_out), .Q(s1_q));  // open: clr
  Clock clock_4 (.out(clock_4_out));
  Register #(.width(32)) v0 (.D(rd_data), .en(demultiplexer_1_out2), .clk(clock_5_out), .Q(v0_q));  // open: clr
  Clock clock_5 (.out(clock_5_out));
  Register #(.width(32)) s2 (.D(rd_data), .en(demultiplexer_1_out18), .clk(clock_6_out), .Q(s2_q));  // open: clr
  Clock clock_6 (.out(clock_6_out));
  Register #(.width(32)) s3 (.D(rd_data), .en(demultiplexer_1_out19), .clk(clock_7_out), .Q(s3_q));  // open: clr
  Clock clock_7 (.out(clock_7_out));
  Register #(.width(32)) v1 (.D(rd_data), .en(demultiplexer_1_out3), .clk(clock_8_out), .Q(v1_q));  // open: clr
  Clock clock_8 (.out(clock_8_out));
  Register #(.width(32)) a0 (.D(rd_data), .en(demultiplexer_1_out4), .clk(clock_9_out), .Q(a0_q));  // open: clr
  Clock clock_9 (.out(clock_9_out));
  Register #(.width(32)) s4 (.D(rd_data), .en(demultiplexer_1_out20), .clk(clock_10_out), .Q(s4_q));  // open: clr
  Clock clock_10 (.out(clock_10_out));
  Register #(.width(32)) a1 (.D(rd_data), .en(demultiplexer_1_out5), .clk(clock_11_out), .Q(a1_q));  // open: clr
  Clock clock_11 (.out(clock_11_out));
  Register #(.width(32)) s5 (.D(rd_data), .en(demultiplexer_1_out21), .clk(clock_12_out), .Q(s5_q));  // open: clr
  Clock clock_12 (.out(clock_12_out));
  Register #(.width(32)) a2 (.D(rd_data), .en(demultiplexer_1_out6), .clk(clock_13_out), .Q(a2_q));  // open: clr
  Clock clock_13 (.out(clock_13_out));
  Register #(.width(32)) s6 (.D(rd_data), .en(demultiplexer_1_out22), .clk(clock_14_out), .Q(s6_q));  // open: clr
  Clock clock_14 (.out(clock_14_out));
  Register #(.width(32)) a3 (.D(rd_data), .en(demultiplexer_1_out7), .clk(clock_15_out), .Q(a3_q));  // open: clr
  Clock clock_15 (.out(clock_15_out));
  Register #(.width(32)) s7 (.D(rd_data), .en(demultiplexer_1_out23), .clk(clock_16_out), .Q(s7_q));  // open: clr
  Clock clock_16 (.out(clock_16_out));
  Register #(.width(32)) t0 (.D(rd_data), .en(demultiplexer_1_out8), .clk(clock_17_out), .Q(t0_q));  // open: clr
  Clock clock_17 (.out(clock_17_out));
  Register #(.width(32)) t8 (.D(rd_data), .en(demultiplexer_1_out24), .clk(clock_18_out), .Q(t8_q));  // open: clr
  Clock clock_18 (.out(clock_18_out));
  Register #(.width(32)) t1 (.D(rd_data), .en(demultiplexer_1_out9), .clk(clock_19_out), .Q(t1_q));  // open: clr
  Clock clock_19 (.out(clock_19_out));
  Register #(.width(32)) t9 (.D(rd_data), .en(demultiplexer_1_out25), .clk(clock_20_out), .Q(t9_q));  // open: clr
  Clock clock_20 (.out(clock_20_out));
  Register #(.width(32)) t2 (.D(rd_data), .en(demultiplexer_1_out10), .clk(clock_21_out), .Q(t2_q));  // open: clr
  Clock clock_21 (.out(clock_21_out));
  Register #(.width(32)) k0 (.D(rd_data), .en(demultiplexer_1_out26), .clk(clock_22_out), .Q(k0_q));  // open: clr
  Clock clock_22 (.out(clock_22_out));
  Register #(.width(32)) k1 (.D(rd_data), .en(demultiplexer_1_out27), .clk(clock_23_out), .Q(k1_q));  // open: clr
  Clock clock_23 (.out(clock_23_out));
  Register #(.width(32)) t3 (.D(rd_data), .en(demultiplexer_1_out11), .clk(clock_24_out), .Q(t3_q));  // open: clr
  Clock clock_24 (.out(clock_24_out));
  Register #(.width(32)) t4 (.D(rd_data), .en(demultiplexer_1_out12), .clk(clock_25_out), .Q(t4_q));  // open: clr
  Clock clock_25 (.out(clock_25_out));
  Register #(.width(32)) gp (.D(rd_data), .en(demultiplexer_1_out28), .clk(clock_26_out), .Q(gp_q));  // open: clr
  Clock clock_26 (.out(clock_26_out));
  Register #(.width(32)) t5 (.D(rd_data), .en(demultiplexer_1_out13), .clk(clock_27_out), .Q(t5_q));  // open: clr
  Clock clock_27 (.out(clock_27_out));
  Register #(.width(32)) sp (.D(rd_data), .en(demultiplexer_1_out29), .clk(clock_28_out), .Q(sp_q));  // open: clr
  Clock clock_28 (.out(clock_28_out));
  Register #(.width(32)) t6 (.D(rd_data), .en(demultiplexer_1_out14), .clk(clock_29_out), .Q(t6_q));  // open: clr
  Clock clock_29 (.out(clock_29_out));
  Register #(.width(32)) s8 (.D(rd_data), .en(demultiplexer_1_out30), .clk(clock_30_out), .Q(s8_q));  // open: clr
  Clock clock_30 (.out(clock_30_out));
  Register #(.width(32)) ra (.D(rd_data), .en(demultiplexer_1_out31), .clk(clock_31_out), .Q(ra_q));  // open: clr
  Clock clock_31 (.out(clock_31_out));
  Register #(.width(32)) t7 (.D(rd_data), .en(demultiplexer_1_out15), .clk(clock_32_out), .Q(t7_q));  // open: clr
  Clock clock_32 (.out(clock_32_out));
  Demultiplexer #(.select(5)) demultiplexer_1 (
    .out0(demultiplexer_1_out0), .out1(demultiplexer_1_out1), .out2(demultiplexer_1_out2),
    .out3(demultiplexer_1_out3), .out4(demultiplexer_1_out4), .out5(demultiplexer_1_out5),
    .out6(demultiplexer_1_out6), .out7(demultiplexer_1_out7), .out8(demultiplexer_1_out8),
    .out9(demultiplexer_1_out9), .out10(demultiplexer_1_out10), .out11(demultiplexer_1_out11),
    .out12(demultiplexer_1_out12), .out13(demultiplexer_1_out13), .out14(demultiplexer_1_out14),
    .out15(demultiplexer_1_out15), .out16(demultiplexer_1_out16), .out17(demultiplexer_1_out17),
    .out18(demultiplexer_1_out18), .out19(demultiplexer_1_out19), .out20(demultiplexer_1_out20),
    .out21(demultiplexer_1_out21), .out22(demultiplexer_1_out22), .out23(demultiplexer_1_out23),
    .out24(demultiplexer_1_out24), .out25(demultiplexer_1_out25), .out26(demultiplexer_1_out26),
    .out27(demultiplexer_1_out27), .out28(demultiplexer_1_out28), .out29(demultiplexer_1_out29),
    .out30(demultiplexer_1_out30), .out31(demultiplexer_1_out31), .in(write), .sel(rd));
endmodule

module ALU (
  input  [3:0] Control,
  input  [31:0] OP1,
  input  [31:0] OP2,
  output [31:0] out_4,
  output Equal
);

  wire clock_1_out, comparator_1_eq, comparator_1_gt, comparator_1_lt, comparator_2_eq, comparator_2_gt,
       comparator_2_lt, multiplexer_1_out, not_1_out, or_1_out, or_2_out;
  wire [4:0] bit_extender_1_out;
  wire [31:0] adder_1_out, divider_1_out, divider_1_rem, HI_q, LO_q, multiplexer_4_out, multiplexer_5_out,
       multiplexer_6_out, multiplexer_8_out, multiplexer_9_out, multiplexer_10_out, multiplexer_11_out,
       multiplexer_12_out, multiplexer_13_out, multiplexer_14_out, multiplexer_15_out, multiplexer_16_out,
       multiplexer_17_out, multiplier_1_cout, multiplier_1_out, shifter_1_out, shifter_2_out,
       subtractor_1_out;

  Comparator #(.width(32)) comparator_1 (
    .a(OP1), .b(OP2), .gt(comparator_1_gt), .eq(comparator_1_eq), .lt(comparator_1_lt));
  Bit_Extender #(.in_width(32), .out_width(5)) bit_extender_1 (.in(OP1), .out(bit_extender_1_out));
  Multiplexer multiplexer_1 (.in0(1'b0), .in1(1'b1), .out(multiplexer_1_out), .sel(comparator_1_eq));
  Comparator #(.width(32)) comparator_2 (
    .a(OP1), .b(OP2), .gt(comparator_2_gt), .eq(comparator_2_eq), .lt(comparator_2_lt));
  or or_1 (or_1_out, comparator_1_gt, comparator_1_lt);
  Multiplexer multiplexer_2 (.in1(1'b0), .out(multiplexer_1_out), .sel(or_1_out));  // open: in0
  not not_1 (not_1_out, multiplexer_1_out);
  Adder #(.width(32)) adder_1 (.a(OP1), .b(OP2), .out(adder_1_out));  // open: cin, cout
  Subtractor #(.width(32)) subtractor_1 (.a(OP1), .b(OP2), .out(subtractor_1_out));  // open: bin, bout
  Shifter #(.width(32)) shifter_1 (.in(OP2), .\dist (bit_extender_1_out), .out(shifter_1_out));
  Shifter #(.shift("lr"), .width(32)) shifter_2 (.in(OP2), .\dist (bit_extender_1_out), .out(shifter_2_out));
  or or_2 (or_2_out, comparator_2_gt, comparator_2_eq);
  Multiplier #(.width(32)) multiplier_1 (
    .a(OP1), .b(OP2), .out(multiplier_1_out), .cout(multiplier_1_cout));  // open: cin
  Divider #(.width(32)) divider_1 (.a(OP1), .b(OP2), .out(divider_1_out), .rem(divider_1_rem));  // open: upper
  Multiplexer #(.select(4)) multiplexer_3 (
    .in0(1'b0), .in1(1'b0), .in2(1'b0), .in3(1'b0), .in4(1'b0), .in5(1'b0), .in6(1'b0), .in7(1'b0),
    .in8(1'b0), .in9(1'b0), .in10(1'b0), .in11(1'b0), .in12(not_1_out), .in13(1'b0),
    .in14(multiplexer_1_out), .in15(1'b0), .out(Equal), .sel(Control));
  Multiplexer #(.width(32)) multiplexer_4 (
    .in0(adder_1_out), .in1(subtractor_1_out), .out(multiplexer_4_out), .sel(Control[0]));
  Multiplexer #(.width(32)) multiplexer_5 (
    .in0(shifter_1_out), .in1(shifter_2_out), .out(multiplexer_5_out), .sel(Control[0]));
  Multiplexer #(.width(32)) multiplexer_6 (.in1(32'h1), .out(multiplexer_6_out), .sel(comparator_2_lt));  // open: in0
  Multiplexer #(.width(32)) multiplexer_7 (.in1({32{1'b0}}), .out(multiplexer_6_out), .sel(or_2_out));  // open: in0
  Multiplexer #(.width(32)) multiplexer_8 (
    .in0(multiplier_1_out), .in1(divider_1_out), .out(multiplexer_8_out), .sel(Control[0]));
  Multiplexer #(.width(32)) multiplexer_9 (
    .in0(multiplier_1_cout), .in1(divider_1_rem), .out(multiplexer_9_out), .sel(Control[0]));
  Multiplexer #(.width(32)) multiplexer_10 (
    .in0(multiplexer_4_out), .in1(multiplexer_5_out), .out(multiplexer_10_out), .sel(Control[1]));
  Multiplexer #(.width(32)) multiplexer_11 (
    .in1(multiplexer_6_out), .out(multiplexer_11_out), .sel(Control[0]));  // open: in0
  Clock clock_1 (.out(clock_1_out));
  Multiplexer #(.width(32)) multiplexer_12 (
    .in0(multiplexer_10_out), .out(multiplexer_12_out), .sel(Control[2]));  // open: in1
  Register #(.width(32)) HI (.D(multiplexer_8_out), .en(Control[3]), .clk(clock_1_out), .Q(HI_q));  // open: clr
  Register #(.width(32)) LO (.D(multiplexer_9_out), .en(Control[3]), .clk(clock_1_out), .Q(LO_q));  // open: clr
  Multiplexer #(.width(32)) multiplexer_13 (
    .in1(multiplexer_11_out), .out(multiplexer_13_out), .sel(Control[1]));  // open: in0
  Multiplexer #(.width(32)) multiplexer_14 (.in0(HI_q), .in1(LO_q), .out(multiplexer_14_out), .sel(Control[0]));
  Multiplexer #(.width(32)) multiplexer_15 (
    .in0(multiplexer_14_out), .out(multiplexer_15_out), .sel(Control[1]));  // open: in1
  Multiplexer #(.width(32)) multiplexer_16 (
    .in0(multiplexer_15_out), .in1(multiplexer_13_out), .out(multiplexer_16_out), .sel(Control[1]));
  Multiplexer #(.width(32)) multiplexer_17 (
    .in0(multiplexer_12_out), .out(multiplexer_17_out), .sel(Control[3]));  // open: in1
  Multiplexer #(.width(32)) multiplexer_18 (
    .in0(multiplexer_17_out), .in1(multiplexer_16_out), .out(out_4), .sel(Control[2]));
endmodule

module Control (
  input  [31:0] Inst,
  output lwSelect,
  output swSelect,
  output beqSelect,
  output bneSelect,
  output jSelect,
  output jalSelect,
  output immSelect,
  output [31:0] SA,
  output [31:0] imm,
  output [4:0] rs,
  output [4:0] rt,
  output [4:0] rd,
  output reg_write_e,
  output shiftSlect,
  output [3:0] ALU_Select,
  output jrSelect,
  output jalr
);

  wire comparator_7_eq, comparator_8_eq, comparator_9_eq, comparator_10_eq, comparator_11_eq,
       comparator_12_eq, comparator_13_eq, comparator_14_eq, comparator_15_eq, comparator_16_eq,
       comparator_17_eq, or_1_out, or_4_out, or_5_out, or_6_out, or_7_out, or_8_out;
  wire [4:0] multiplexer_2_out;
  wire [5:0] multiplexer_1_out;
  wire [31:0] adder_1_out, bit_extender_1_out, bit_extender_3_out, multiplexer_16_out;

  or or_1 (or_1_out, swSelect, beqSelect, bneSelect, jSelect);
  Multiplexer #(.width(6)) multiplexer_1 (
    .in0({6{1'b1}}), .in1(Inst[5:0]), .out(multiplexer_1_out), .sel(comparator_7_eq));
  Comparator #(.width(6)) comparator_1 (.a(6'b100011), .b(Inst[31:26]), .eq(lwSelect));  // open: gt, lt
  Comparator #(.width(6)) comparator_2 (.a(6'b101011), .b(Inst[31:26]), .eq(swSelect));  // open: gt, lt
  Comparator #(.width(6)) comparator_3 (.a(6'b000100), .b(Inst[31:26]), .eq(beqSelect));  // open: gt, lt
  Comparator #(.width(6)) comparator_4 (.a(6'b000101), .b(Inst[31:26]), .eq(bneSelect));  // open: gt, lt
  Comparator #(.width(6)) comparator_5 (.a(6'b000010), .b(Inst[31:26]), .eq(jSelect));  // open: gt, lt
  Comparator #(.width(6)) comparator_6 (.a(6'b000011), .b(Inst[31:26]), .eq(jalSelect));  // open: gt, lt
  Comparator #(.width(6)) comparator_7 (.a({6{1'b0}}), .b(Inst[31:26]), .eq(comparator_7_eq));  // open: gt, lt
  Comparator #(.width(6)) comparator_8 (.a(6'b001000), .b(Inst[31:26]), .eq(comparator_8_eq));  // open: gt, lt
  Comparator #(.width(6)) comparator_9 (.a(multiplexer_1_out), .b(6'b011010), .eq(comparator_9_eq));  // open: gt, lt
  Comparator #(.width(6)) comparator_10 (.a(multiplexer_1_out), .b(6'b011000), .eq(comparator_10_eq));  // open: gt, lt
  Comparator #(.width(6)) comparator_11 (.a(multiplexer_1_out), .b(6'b010010), .eq(comparator_11_eq));  // open: gt, lt
  Comparator #(.width(6)) comparator_12 (.a(multiplexer_1_out), .b(6'b010000), .eq(comparator_12_eq));  // open: gt, lt
  Comparator #(.width(6)) comparator_13 (.a(multiplexer_1_out), .b({6{1'b0}}), .eq(comparator_13_eq));  // open: gt, lt
  Comparator #(.width(6)) comparator_14 (.a(multiplexer_1_out), .b(6'b000010), .eq(comparator_14_eq));  // open: gt, lt
  Comparator #(.width(6)) comparator_15 (.a(multiplexer_1_out), .b(6'b100000), .eq(comparator_15_eq));  // open: gt, lt
  Comparator #(.width(6)) comparator_16 (.a(multiplexer_1_out), .b(6'b100010), .eq(comparator_16_eq));  // open: gt, lt
  Comparator #(.width(6)) comparator_17 (.a(multiplexer_1_out), .b(6'b101010), .eq(comparator_17_eq));  // open: gt, lt
  Comparator #(.width(6)) comparator_18 (.a(multiplexer_1_out), .b(6'b001000), .eq(jrSelect));  // open: gt, lt
  Comparator #(.width(6)) comparator_19 (.a(multiplexer_1_out), .b(6'b001001), .eq(jalr));  // open: gt, lt
  or or_2 (immSelect, jalSelect, swSelect, lwSelect, jalr, comparator_8_eq);
  or or_3 (shiftSlect, comparator_13_eq, comparator_14_eq);
  or or_4 (or_4_out, lwSelect, comparator_8_eq);
  Multiplexer #(.width(5)) multiplexer_2 (
    .in0(Inst[15:11]), .in1(Inst[20:16]), .out(multiplexer_2_out), .sel(or_4_out));
  or or_5 (or_5_out, comparator_9_eq, or_1_out, jrSelect, comparator_10_eq);
  Multiplexer #(.width(4)) multiplexer_3 (.in1(4'b1110), .out(ALU_Select), .sel(beqSelect));  // open: in0
  Multiplexer #(.width(4)) multiplexer_4 (.in1(4'b1100), .out(ALU_Select), .sel(bneSelect));  // open: in0
  or or_6 (or_6_out, jalSelect, jalr);
  Multiplexer #(.width(5)) multiplexer_5 (.in0(multiplexer_2_out), .in1({5{1'b1}}), .out(rd), .sel(or_6_out));
  Multiplexer #(.width(4)) multiplexer_6 (.in1(4'b0000), .out(ALU_Select), .sel(comparator_8_eq));  // open: in0
  Multiplexer #(.width(4)) multiplexer_7 (.in1(4'b1001), .out(ALU_Select), .sel(comparator_9_eq));  // open: in0
  Multiplexer #(.width(4)) multiplexer_8 (.in1(4'b1000), .out(ALU_Select), .sel(comparator_10_eq));  // open: in0
  Multiplexer #(.width(4)) multiplexer_9 (.in1(4'b0100), .out(ALU_Select), .sel(comparator_11_eq));  // open: in0
  Multiplexer #(.width(4)) multiplexer_10 (.in1(4'b0101), .out(ALU_Select), .sel(comparator_12_eq));  // open: in0
  Multiplexer #(.width(4)) multiplexer_11 (.in1(4'b0010), .out(ALU_Select), .sel(comparator_13_eq));  // open: in0
  Multiplexer #(.width(4)) multiplexer_12 (.in1(4'b0011), .out(ALU_Select), .sel(comparator_14_eq));  // open: in0
  Multiplexer #(.width(4)) multiplexer_13 (.in1(4'b0000), .out(ALU_Select), .sel(comparator_15_eq));  // open: in0
  Multiplexer #(.width(4)) multiplexer_14 (.in1(4'b0001), .out(ALU_Select), .sel(comparator_16_eq));  // open: in0
  Multiplexer #(.width(4)) multiplexer_15 (.in1(4'b1111), .out(ALU_Select), .sel(comparator_17_eq));  // open: in0
  assign bit_extender_1_out = {{16{Inst[15]}}, Inst[15:0]};  // Bit_Extender bit_extender_1
  assign SA = {{27{Inst[10]}}, Inst[10:6]};  // Bit_Extender bit_extender_2
  or or_7 (or_7_out, lwSelect, swSelect);
  or or_8 (or_8_out, jSelect, jalSelect);
  not not_1 (reg_write_e, or_5_out);
  assign bit_extender_3_out = {{27{1'b0}}, Inst[25:21]};  // Bit_Extender bit_extender_3
  Multiplexer #(.width(32)) multiplexer_16 (
    .in0({32{1'b0}}), .in1(bit_extender_3_out), .out(multiplexer_16_out), .sel(or_7_out));
  Adder #(.width(32)) adder_1 (.a(multiplexer_16_out), .b(bit_extender_1_out), .out(adder_1_out));  // open: cin, cout
  Multiplexer #(.width(32)) multiplexer_17 (
    .in0(adder_1_out), .in1({{6{1'b0}}, Inst[25:0]}), .out(imm), .sel(or_8_out));

  assign rs = Inst[25:21];
  assign rt = Inst[20:16];

  // Notes on the sheet:
  //   opcodes...
  //   lw
  //   sw
  //   beq
  //   bne
  //   j
  //   jal
  //   addi
  //   div
  //   mult
  //   mflo
  //   mfhi
  //   sll
  //   srl
  //   add
  //   sub
  //   slt
  //   jr
  //   jalr
  //   target
  //   reg write
  //   rt as rd
  //   ra as rd
  //   offset
  //   target
  //   imm/offset/target
endmodule
