// Logisim project project4.circ as structural Verilog: 11 circuits, main circuit Computer
module CPU (
  input  [31:0] DataFromBus,
  output BusWriteEnable,
  output [25:0] AddressToBus,
  output [31:0] DataToBus
);

  wire alu_1_equal, and_1_out, and_2_out, clock_1_out, control_1_beqsel, control_1_bnesel, control_1_immsel,
       control_1_jalrsel, control_1_jalsel, control_1_jrsel, control_1_jsel, control_1_lwsel,
       control_1_regwritee, control_1_shiftsel, not_1_out, or_1_out, or_2_out, or_3_out, or_4_out;
  wire [3:0] control_1_alucode;
  wire [4:0] control_1_rd, control_1_rs, control_1_rt;
  wire [15:0] bit_extender_1_out;
  wire [31:0] adder_1_out, adder_2_out, alu_1_res, control_1_imm, control_1_shiftamount, multiplexer_1_out,
       multiplexer_2_out, multiplexer_3_out, multiplexer_4_out, multiplexer_5_out, multiplexer_6_out,
       multiplexer_7_out, regfile_1_rs_data, register_1_q, rom_1_data, shifter_1_out, shifter_2_out,
       shifter_3_out;

  // Probe on register_1_q
  Adder #(.width(32)) adder_1 (.a(register_1_q), .b(32'h4), .out(adder_1_out));  // open: cin, cout
  Shifter #(.width(32)) shifter_1 (.in(control_1_imm), .\dist (5'b00010), .out(shifter_1_out));
  Adder #(.width(32)) adder_2 (.a(adder_1_out), .b(shifter_1_out), .out(adder_2_out));  // open: cin, cout
  Shifter #(.width(32)) shifter_2 (.in(control_1_imm), .\dist (5'b00010), .out(shifter_2_out));
  Multiplexer #(.width(32)) multiplexer_1 (
    .in0(adder_1_out), .in1(adder_2_out), .out(multiplexer_1_out), .sel(or_3_out));
  Multiplexer #(.width(32)) multiplexer_2 (
    .in0(shifter_2_out), .in1(regfile_1_rs_data), .out(multiplexer_2_out), .sel(or_1_out));
  // Probe on multiplexer_3_out
  Register #(.width(32)) register_1 (
    .D(multiplexer_3_out), .en(1'b1), .clk(clock_1_out), .Q(register_1_q));  // open: clr
  Multiplexer #(.width(32)) multiplexer_3 (
    .in0(multiplexer_1_out), .in1(multiplexer_2_out), .out(multiplexer_3_out), .sel(or_2_out));
  Clock clock_1 (.out(clock_1_out));
  // Probe on control_1_imm
  Shifter #(.shift("ar"), .width(32)) shifter_3 (.in(register_1_q), .\dist (5'b00010), .out(shifter_3_out));
  Bit_Extender #(.in_width(32)) bit_extender_1 (.in(shifter_3_out), .out(bit_extender_1_out));
  // Probe on bit_extender_1_out
  ROM #(.addrWidth(16), .dataWidth(32)) rom_1 (.addr(bit_extender_1_out), .data(rom_1_data));
  // Probe on adder_1_out
  Multiplexer #(.width(32)) multiplexer_4 (
    .in0(multiplexer_7_out), .in1(adder_1_out), .out(multiplexer_4_out), .sel(or_4_out));
  // Probe on regfile_1_rs_data
  or or_1 (or_1_out, control_1_jrsel, control_1_jalrsel);
  // Probe on control_1_rd
  or or_2 (or_2_out, control_1_jalsel, control_1_jsel, control_1_jalrsel, control_1_jrsel);
  // Probe on control_1_imm
  // Probe on control_1_rs
  regfile regfile_1 (
    .rd_data(multiplexer_4_out), .write_e(control_1_regwritee), .rt(control_1_rt), .rs(control_1_rs),
    .rd(control_1_rd), .rs_data(regfile_1_rs_data), .rt_data(DataToBus));
  or or_3 (or_3_out, and_1_out, and_2_out);
  Control control_1 (
    .Inst(rom_1_data), .ALUCode(control_1_alucode), .jrSel(control_1_jrsel), .jalrSel(control_1_jalrsel),
    .shiftSel(control_1_shiftsel), .shiftAmount(control_1_shiftamount), .rd(control_1_rd), .rt(control_1_rt),
    .rs(control_1_rs), .imm(control_1_imm), .lwSel(control_1_lwsel), .swSel(BusWriteEnable),
    .beqSel(control_1_beqsel), .bneSel(control_1_bnesel), .immSel(control_1_immsel), .jSel(control_1_jsel),
    .jalSel(control_1_jalsel), .regWriteE(control_1_regwritee));
  // Probe on control_1_rt
  Multiplexer #(.width(32)) multiplexer_5 (
    .in0(DataToBus), .in1(control_1_imm), .out(multiplexer_5_out), .sel(control_1_immsel));
  // Probe on multiplexer_7_out
  and and_1 (and_1_out, control_1_bnesel, not_1_out);
  and and_2 (and_2_out, alu_1_equal, control_1_beqsel);
  Multiplexer #(.width(32)) multiplexer_6 (
    .in0(regfile_1_rs_data), .in1(control_1_shiftamount), .out(multiplexer_6_out), .sel(control_1_shiftsel));
  not not_1 (not_1_out, alu_1_equal);
  or or_4 (or_4_out, control_1_jalrsel, control_1_jalsel);
  // Probe on multiplexer_6_out
  // Probe on multiplexer_5_out
  ALU alu_1 (
    .op2(multiplexer_5_out), .op1(multiplexer_6_out), .ALUCode(control_1_alucode), .res(alu_1_res),
    .equal(alu_1_equal));
  Multiplexer #(.width(32)) multiplexer_7 (
    .in0(alu_1_res), .in1(DataFromBus), .out(multiplexer_7_out), .sel(control_1_lwsel));
  Bit_Extender #(.in_width(32), .out_width(26)) bit_extender_2 (.in(alu_1_res), .out(AddressToBus));

  // Notes on the sheet:
  //   offset
  //   pc+4
  //   offset
  //   rd_data
  //   branchSelect
  //   branchSelect
  //   jSelect
  //   ProgramCounter
  //   contents of rom_1 (hex, n*v repeats v):
  //   10400011 201b0001 105b0013 201b0004 105b0085 201b0005 105b0028 201b0008 105b0087 201b0009 105b0072
  //   201b000a 105b0075 201b000b 105b0074 201b000c 105bffef 8000082 23bdf000 201b0000 ac1bf000 80000a5
  //   23bdfff4 23bb0000 afba0008 afaa0004 afab0000 200a000a 209a0000 34a001a d012 5810 23bdfffc afab0000
  //   1740fffa 8fba0000 235a0030 ac1aff00 23bd0004 17bbfffb 8fab0000 23bd0004 8faa0000 23bd0004 8fba0000
  //   23bd0004 3400008 23bdfff4 afaa0000 afab0004 afba0008 200a000a 201b0000 200b0030 8c1aff10 1340fff7
  //   8c1aff14 ac00ff10 134b0014 216b0001 134b0014 216b0001 134b0016 216b0001 134b0018 216b0001 134b001a
  //   216b0001 134b001c 216b0001 134b001e 216b0001 134b0020 216b0001 134b0022 216b0001 134b0024 1ad820
  //   8000075 36a0018 d812 36a0018 d812 237b0001 8000075 36a0018 d812 237b0002 8000075 36a0018 d812
  //   237b0003 8000075 36a0018 d812 237b0004 8000075 36a0018 d812 237b0005 8000075 36a0018 d812 237b0006
  //   8000075 36a0018 d812 237b0007 8000075 36a0018 d812 237b0008 8000075 36a0018 d812 237b0009 8000075
  //   3601020 8faa0000 23bd0004 8fab0000 23bd0004 8fba0000 23bd0004 3400008 209b0000 8c02f000 362d820
  //   ac1bf000 3400008 8000082 ac04ff00 3400008 8c1bff10 1360fffe 8c02ff14 ac00ff10 3400008 8c9b0000
  //   13600003 ac1bff00 20840004 800008a 3400008 23bdfffc afaa0000 200a0000 8c1aff10 1340fffb 8c1aff14
  //   ac00ff10 201b000a 135b0004 23bdfffc 214a0004 afba0000 8000093 23bdfffc 214a0004 afa00000 3aae820
  //   ac1df000 8faa0000 23bd0004 3400008 20100001 20150000 200d0000 2011000a 20020005 d00c 20520000
  //   251982a 12600006 2500018 9012 2110018 8012 2b2a820 80000a8 12a00008 2011000a 2b1001a a812 5810
  //   1b10018 6812 1ab6820 80000b4 1a0a820 2014005f 12d4000e 1254000d 2014002b 12d40018 12540017 2014002d
  //   12d40024 12540023 2014002a 12d40030 1254002f 2014002f 12d4003e 1254003d 80000a5 200e002b 12ce0013
  //   124e0012 200e002d 12ce001f 124e001e 200e002a 12ce002c 124e002b 200e002f 12ce003a 124e0039 80000a5
  //   22b70000 c00011b 21be0000 3d77820 3d72020 20020001 d00c 80000a5 c00011b 21be0000 1fe2020 20020001
  //   d00c 1fe7820 80000a5 22b70000 c00011b 21be0000 2fe7822 2fe2022 20020001 d00c 80000a5 c00011b
  //   21be0000 1fe2022 20020001 d00c 1fe7822 80000a5 22b70000 c00011b 21be0000 2fe0018 7812 f2020 20020001
  //   d00c 80000a5 c00011b 21be0000 1fe0018 2012 20020001 d00c 47820 80000a5 22b70000 c00011b 21be0000
  //   2fe001a 7812 f2020 20020001 d00c 80000a5 c00011b 21be0000 1fe001a 2012 20020001 d00c 47820 80000a5
  //   20100001 20150000 200d0000 2011000a 20020005 d00c 20520000 251982a 12600006 2500018 9012 2110018
  //   8012 2b2a820 800011e 12a00008 2011000a 2b1001a a812 5810 1b10018 6812 1ab6820 800012a 240b020
  //   3e00008
  //   jr/jalr
  //   j-type
  //   branch
  //   immSel
  //   bne
  //   beq
  //   shiftSel
  //   jalr/jal
endmodule

module regfile (
  input  [31:0] rd_data,
  input  [4:0] rd,
  input  write_e,
  input  [4:0] rs,
  input  [4:0] rt,
  output [31:0] rs_data,
  output [31:0] rt_data
);

  wire and_1_out, clock_1_out, demultiplexer_1_out0, demultiplexer_1_out1, demultiplexer_1_out2,
       demultiplexer_1_out3, demultiplexer_1_out4, demultiplexer_1_out5, demultiplexer_1_out6,
       demultiplexer_1_out7, demultiplexer_1_out8, demultiplexer_1_out9, demultiplexer_1_out10,
       demultiplexer_1_out11, demultiplexer_1_out12, demultiplexer_1_out13, demultiplexer_1_out14,
       demultiplexer_1_out15, demultiplexer_1_out16, demultiplexer_1_out17, demultiplexer_1_out18,
       demultiplexer_1_out19, demultiplexer_1_out20, demultiplexer_1_out21, demultiplexer_1_out22,
       demultiplexer_1_out23, demultiplexer_1_out24, demultiplexer_1_out25, demultiplexer_1_out26,
       demultiplexer_1_out27, demultiplexer_1_out28, demultiplexer_1_out29, demultiplexer_1_out30,
       demultiplexer_1_out31;
  wire [31:0] R0_q, R1_q, R2_q, R3_q, R4_q, R5_q, R6_q, R7_q, R8_q, R9_q, R10_q, R11_q, R12_q, R13_q, R14_q,
       R15_q, R16_q, R17_q, R18_q, R19_q, R20_q, R21_q, R22_q, R23_q, R24_q, R25_q, R26_q, R27_q, R28_q,
       R29_q, R30_q, R31_q;

  Clock clock_1 (.out(clock_1_out));
  Demultiplexer #(.select(5)) demultiplexer_1 (
    .out0(demultiplexer_1_out0), .out1(demultiplexer_1_out1), .out2(demultiplexer_1_out2),
    .out3(demultiplexer_1_out3), .out4(demultiplexer_1_out4), .out5(demultiplexer_1_out5),
    .out6(demultiplexer_1_out6), .out7(demultiplexer_1_out7), .out8(demultiplexer_1_out8),
    .out9(demultiplexer_1_out9), .out10(demultiplexer_1_out10), .out11(demultiplexer_1_out11),
    .out12(demultiplexer_1_out12), .out13(demultiplexer_1_out13), .out14(demultiplexer_1_out14),
    .out15(demultiplexer_1_out15), .out16(demultiplexer_1_out16), .out17(demultiplexer_1_out17),
    .out18(demultiplexer_1_out18), .out19(demultiplexer_1_out19), .out20(demultiplexer_1_out20),
    .out21(demultiplexer_1_out21), .out22(demultiplexer_1_out22), .out23(demultiplexer_1_out23),
    .out24(demultiplexer_1_out24), .out25(demultiplexer_1_out25), .out26(demultiplexer_1_out26),
    .out27(demultiplexer_1_out27), .out28(demultiplexer_1_out28), .out29(demultiplexer_1_out29),
    .out30(demultiplexer_1_out30), .out31(demultiplexer_1_out31), .in(write_e), .sel(rd));
  Register #(.width(32)) R1 (.D(rd_data), .en(demultiplexer_1_out1), .clk(clock_1_out), .Q(R1_q));  // open: clr
  Register #(.width(32)) R2 (.D(rd_data), .en(demultiplexer_1_out2), .clk(clock_1_out), .Q(R2_q));  // open: clr
  Register #(.width(32)) R3 (.D(rd_data), .en(demultiplexer_1_out3), .clk(clock_1_out), .Q(R3_q));  // open: clr
  Register #(.width(32)) R4 (.D(rd_data), .en(demultiplexer_1_out4), .clk(clock_1_out), .Q(R4_q));  // open: clr
  Register #(.width(32)) R5 (.D(rd_data), .en(demultiplexer_1_out5), .clk(clock_1_out), .Q(R5_q));  // open: clr
  Register #(.width(32)) R6 (.D(rd_data), .en(demultiplexer_1_out6), .clk(clock_1_out), .Q(R6_q));  // open: clr
  Register #(.width(32)) R7 (.D(rd_data), .en(demultiplexer_1_out7), .clk(clock_1_out), .Q(R7_q));  // open: clr
  Register #(.width(32)) R8 (.D(rd_data), .en(demultiplexer_1_out8), .clk(clock_1_out), .Q(R8_q));  // open: clr
  Register #(.width(32)) R9 (.D(rd_data), .en(demultiplexer_1_out9), .clk(clock_1_out), .Q(R9_q));  // open: clr
  Register #(.width(32)) R10 (.D(rd_data), .en(demultiplexer_1_out10), .clk(clock_1_out), .Q(R10_q));  // open: clr
  Register #(.width(32)) R11 (.D(rd_data), .en(demultiplexer_1_out11), .clk(clock_1_out), .Q(R11_q));  // open: clr
  Register #(.width(32)) R12 (.D(rd_data), .en(demultiplexer_1_out12), .clk(clock_1_out), .Q(R12_q));  // open: clr
  Register #(.width(32)) R13 (.D(rd_data), .en(demultiplexer_1_out13), .clk(clock_1_out), .Q(R13_q));  // open: clr
  Register #(.width(32)) R14 (.D(rd_data), .en(demultiplexer_1_out14), .clk(clock_1_out), .Q(R14_q));  // open: clr
  Register #(.width(32)) R15 (.D(rd_data), .en(demultiplexer_1_out15), .clk(clock_1_out), .Q(R15_q));  // open: clr
  Register #(.width(32)) R16 (.D(rd_data), .en(demultiplexer_1_out16), .clk(clock_1_out), .Q(R16_q));  // open: clr
  Register #(.width(32)) R17 (.D(rd_data), .en(demultiplexer_1_out17), .clk(clock_1_out), .Q(R17_q));  // open: clr
  Register #(.width(32)) R18 (.D(rd_data), .en(demultiplexer_1_out18), .clk(clock_1_out), .Q(R18_q));  // open: clr
  Register #(.width(32)) R19 (.D(rd_data), .en(demultiplexer_1_out19), .clk(clock_1_out), .Q(R19_q));  // open: clr
  Register #(.width(32)) R20 (.D(rd_data), .en(demultiplexer_1_out20), .clk(clock_1_out), .Q(R20_q));  // open: clr
  Register #(.width(32)) R21 (.D(rd_data), .en(demultiplexer_1_out21), .clk(clock_1_out), .Q(R21_q));  // open: clr
  Register #(.width(32)) R22 (.D(rd_data), .en(demultiplexer_1_out22), .clk(clock_1_out), .Q(R22_q));  // open: clr
  Register #(.width(32)) R23 (.D(rd_data), .en(demultiplexer_1_out23), .clk(clock_1_out), .Q(R23_q));  // open: clr
  Register #(.width(32)) R24 (.D(rd_data), .en(demultiplexer_1_out24), .clk(clock_1_out), .Q(R24_q));  // open: clr
  Register #(.width(32)) R25 (.D(rd_data), .en(demultiplexer_1_out25), .clk(clock_1_out), .Q(R25_q));  // open: clr
  Register #(.width(32)) R26 (.D(rd_data), .en(demultiplexer_1_out26), .clk(clock_1_out), .Q(R26_q));  // open: clr
  Register #(.width(32)) R27 (.D(rd_data), .en(demultiplexer_1_out27), .clk(clock_1_out), .Q(R27_q));  // open: clr
  Register #(.width(32)) R28 (.D(rd_data), .en(demultiplexer_1_out28), .clk(clock_1_out), .Q(R28_q));  // open: clr
  Register #(.width(32)) R29 (.D(rd_data), .en(demultiplexer_1_out29), .clk(clock_1_out), .Q(R29_q));  // open: clr
  Register #(.width(32)) R30 (.D(rd_data), .en(demultiplexer_1_out30), .clk(clock_1_out), .Q(R30_q));  // open: clr
  and and_1 (and_1_out, demultiplexer_1_out0, 1'b0);
  Register #(.width(32)) R31 (.D(rd_data), .en(demultiplexer_1_out31), .clk(clock_1_out), .Q(R31_q));  // open: clr
  Register #(.width(32)) R0 (.D(rd_data), .en(and_1_out), .clk(clock_1_out), .Q(R0_q));  // open: clr
  Multiplexer #(.select(5), .width(32)) multiplexer_1 (
    .in0(R0_q), .in1(R1_q), .in2(R2_q), .in3(R3_q), .in4(R4_q), .in5(R5_q), .in6(R6_q), .in7(R7_q),
    .in8(R8_q), .in9(R9_q), .in10(R10_q), .in11(R11_q), .in12(R12_q), .in13(R13_q), .in14(R14_q),
    .in15(R15_q), .in16(R16_q), .in17(R17_q), .in18(R18_q), .in19(R19_q), .in20(R20_q), .in21(R21_q),
    .in22(R22_q), .in23(R23_q), .in24(R24_q), .in25(R25_q), .in26(R26_q), .in27(R27_q), .in28(R28_q),
    .in29(R29_q), .in30(R30_q), .in31(R31_q), .out(rs_data), .sel(rs));
  Multiplexer #(.select(5), .width(32)) multiplexer_2 (
    .in0(R0_q), .in1(R1_q), .in2(R2_q), .in3(R3_q), .in4(R4_q), .in5(R5_q), .in6(R6_q), .in7(R7_q),
    .in8(R8_q), .in9(R9_q), .in10(R10_q), .in11(R11_q), .in12(R12_q), .in13(R13_q), .in14(R14_q),
    .in15(R15_q), .in16(R16_q), .in17(R17_q), .in18(R18_q), .in19(R19_q), .in20(R20_q), .in21(R21_q),
    .in22(R22_q), .in23(R23_q), .in24(R24_q), .in25(R25_q), .in26(R26_q), .in27(R27_q), .in28(R28_q),
    .in29(R29_q), .in30(R30_q), .in31(R31_q), .out(rt_data), .sel(rt));
endmodule

module ALU (
  input  [3:0] ALUCode,
  input  [31:0] op1,
  input  [31:0] op2,
  output [31:0] res,
  output equal
);

  wire clock_1_out, clock_2_out, comparator_2_lt, comparator_3_eq, comparator_3_gt, or_1_out;
  wire [4:0] bit_extender_1_out, bit_extender_2_out;
  wire [31:0] adder_1_out, bit_extender_3_out, divider_1_out, divider_1_rem, HI_q, LO_q, multiplexer_1_out,
       multiplexer_2_out, multiplier_1_cout, multiplier_1_out, shifter_1_out, shifter_2_out, subtractor_1_out;

  Comparator #(.width(32)) comparator_1 (.a(op1), .b(op2), .eq(equal));  // open: gt, lt
  Adder #(.width(32)) adder_1 (.a(op1), .b(op2), .out(adder_1_out));  // open: cin, cout
  Subtractor #(.width(32)) subtractor_1 (.a(op1), .b(op2), .out(subtractor_1_out));  // open: bin, bout
  Divider #(.width(32)) divider_1 (.a(op1), .b(op2), .out(divider_1_out), .rem(divider_1_rem));  // open: upper
  Multiplier #(.width(32)) multiplier_1 (
    .a(op1), .b(op2), .out(multiplier_1_out), .cout(multiplier_1_cout));  // open: cin
  Bit_Extender #(.in_width(32), .out_width(5)) bit_extender_1 (.in(op1), .out(bit_extender_1_out));
  Bit_Extender #(.in_width(32), .out_width(5)) bit_extender_2 (.in(op1), .out(bit_extender_2_out));
  Comparator #(.width(32)) comparator_2 (.a(op1), .b(op2), .lt(comparator_2_lt));  // open: gt, eq
  Shifter #(.width(32)) shifter_1 (.in(op2), .\dist (bit_extender_1_out), .out(shifter_1_out));
  Shifter #(.shift("lr"), .width(32)) shifter_2 (.in(op2), .\dist (bit_extender_2_out), .out(shifter_2_out));
  Comparator #(.mode("unsigned"), .width(4)) comparator_3 (
    .a(ALUCode), .b(4'b1000), .gt(comparator_3_gt), .eq(comparator_3_eq));  // open: lt
  or or_1 (or_1_out, comparator_3_eq, comparator_3_gt);
  assign bit_extender_3_out = {{31{1'b0}}, comparator_2_lt};  // Bit_Extender bit_extender_3
  Multiplexer #(.width(32)) multiplexer_1 (
    .in0(multiplier_1_out), .in1(divider_1_out), .out(multiplexer_1_out), .sel(comparator_3_gt));
  Multiplexer #(.width(32)) multiplexer_2 (
    .in0(multiplier_1_cout), .in1(divider_1_rem), .out(multiplexer_2_out), .sel(comparator_3_gt));
  Register #(.width(32)) LO (.D(multiplexer_1_out), .en(or_1_out), .clk(clock_1_out), .Q(LO_q));  // open: clr
  Clock clock_1 (.out(clock_1_out));
  Register #(.width(32)) HI (.D(multiplexer_2_out), .en(or_1_out), .clk(clock_2_out), .Q(HI_q));  // open: clr
  Clock clock_2 (.out(clock_2_out));
  Multiplexer #(.select(4), .width(32)) multiplexer_3 (
    .in0(adder_1_out), .in1(subtractor_1_out), .in2(LO_q), .in3(HI_q), .in4(shifter_1_out),
    .in5(shifter_2_out), .in7(bit_extender_3_out), .out(res), .sel(ALUCode));  // open: in6, in8, in9, in10, in11, in12, in13, in14, in15

  // Notes on the sheet:
  //   op2 only
  //   add
  //   sub
  //   div
  //   mult
  //   sll
  //   srl
endmodule

module Control (
  input  [31:0] Inst,
  output [3:0] ALUCode,
  output jrSel,
  output jalrSel,
  output shiftSel,
  output [31:0] shiftAmount,
  output [4:0] rd,
  output [4:0] rt,
  output [4:0] rs,
  output [31:0] imm,
  output lwSel,
  output swSel,
  output beqSel,
  output bneSel,
  output immSel,
  output jSel,
  output jalSel,
  output regWriteE
);

  wire comparator_1_eq, comparator_2_eq, comparator_9_eq, comparator_11_eq, comparator_12_eq,
       comparator_13_eq, comparator_14_eq, comparator_15_eq, comparator_16_eq, comparator_17_eq,
       comparator_18_eq, comparator_19_eq, comparator_20_eq, or_1_out, or_2_out, or_4_out, or_5_out, or_7_out;
  wire [4:0] multiplexer_2_out, multiplexer_13_out;
  wire [5:0] multiplexer_1_out;
  wire [31:0] bit_extender_2_out;

  Comparator #(.width(6)) comparator_1 (.a(Inst[31:26]), .b({6{1'b0}}), .eq(comparator_1_eq));  // open: gt, lt
  Multiplexer #(.width(6)) multiplexer_1 (
    .in0(6'b001111), .in1(Inst[5:0]), .out(multiplexer_1_out), .sel(comparator_1_eq));
  Comparator #(.width(6)) comparator_2 (.a(Inst[31:26]), .b(6'b001000), .eq(comparator_2_eq));  // open: gt, lt
  Comparator #(.width(6)) comparator_3 (.a(Inst[31:26]), .b(6'b100011), .eq(lwSel));  // open: gt, lt
  Comparator #(.width(6)) comparator_4 (.a(Inst[31:26]), .b(6'b101011), .eq(swSel));  // open: gt, lt
  Comparator #(.width(6)) comparator_5 (.a(Inst[31:26]), .b(6'b000100), .eq(beqSel));  // open: gt, lt
  Comparator #(.width(6)) comparator_6 (.a(Inst[31:26]), .b(6'b000101), .eq(bneSel));  // open: gt, lt
  Comparator #(.width(6)) comparator_7 (.a(Inst[31:26]), .b(6'b000010), .eq(jSel));  // open: gt, lt
  Comparator #(.width(6)) comparator_8 (.a(Inst[31:26]), .b(6'b000011), .eq(jalSel));  // open: gt, lt
  Comparator #(.width(6)) comparator_9 (.a(multiplexer_1_out), .b(6'b001100), .eq(comparator_9_eq));  // open: gt, lt
  Comparator #(.width(6)) comparator_10 (.a(multiplexer_1_out), .b(6'b001000), .eq(jrSel));  // open: gt, lt
  Comparator #(.width(6)) comparator_11 (.a(multiplexer_1_out), .b(6'b001001), .eq(comparator_11_eq));  // open: gt, lt
  Comparator #(.width(6)) comparator_12 (.a(multiplexer_1_out), .b(6'b101010), .eq(comparator_12_eq));  // open: gt, lt
  Comparator #(.width(6)) comparator_13 (.a(multiplexer_1_out), .b(6'b010010), .eq(comparator_13_eq));  // open: gt, lt
  Comparator #(.width(6)) comparator_14 (.a(multiplexer_1_out), .b(6'b010000), .eq(comparator_14_eq));  // open: gt, lt
  Comparator #(.width(6)) comparator_15 (.a(multiplexer_1_out), .b({6{1'b0}}), .eq(comparator_15_eq));  // open: gt, lt
  Comparator #(.width(6)) comparator_16 (.a(multiplexer_1_out), .b(6'b000010), .eq(comparator_16_eq));  // open: gt, lt
  Comparator #(.width(6)) comparator_17 (.a(multiplexer_1_out), .b(6'b011000), .eq(comparator_17_eq));  // open: gt, lt
  Comparator #(.width(6)) comparator_18 (.a(multiplexer_1_out), .b(6'b011010), .eq(comparator_18_eq));  // open: gt, lt
  Comparator #(.width(6)) comparator_19 (.a(multiplexer_1_out), .b(6'b100000), .eq(comparator_19_eq));  // open: gt, lt
  Comparator #(.width(6)) comparator_20 (.a(multiplexer_1_out), .b(6'b100010), .eq(comparator_20_eq));  // open: gt, lt
  Multiplexer #(.width(5)) multiplexer_2 (
    .in0(Inst[15:11]), .in1(Inst[20:16]), .out(multiplexer_2_out), .sel(or_1_out));
  or or_1 (or_1_out, comparator_2_eq, lwSel);
  or or_2 (or_2_out, jSel, jalSel);
  or or_3 (shiftSel, comparator_15_eq, comparator_16_eq);
  or or_4 (or_4_out, comparator_17_eq, comparator_18_eq);
  Multiplexer #(.width(4)) multiplexer_3 (.in1(4'b0111), .out(ALUCode), .sel(comparator_12_eq));  // open: in0
  Multiplexer #(.width(4)) multiplexer_4 (.in1(4'b0010), .out(ALUCode), .sel(comparator_13_eq));  // open: in0
  Multiplexer #(.width(4)) multiplexer_5 (.in1(4'b0011), .out(ALUCode), .sel(comparator_14_eq));  // open: in0
  Multiplexer #(.width(4)) multiplexer_6 (.in1(4'b0100), .out(ALUCode), .sel(comparator_15_eq));  // open: in0
  Multiplexer #(.width(4)) multiplexer_7 (.in1(4'b0101), .out(ALUCode), .sel(comparator_16_eq));  // open: in0
  Multiplexer #(.width(4)) multiplexer_8 (.in1(4'b1000), .out(ALUCode), .sel(comparator_17_eq));  // open: in0
  Multiplexer #(.width(4)) multiplexer_9 (.in1(4'b1001), .out(ALUCode), .sel(comparator_18_eq));  // open: in0
  Multiplexer #(.width(4)) multiplexer_10 (.in1(4'b0000), .out(ALUCode), .sel(comparator_19_eq));  // open: in0
  Multiplexer #(.width(4)) multiplexer_11 (.in1(4'b0001), .out(ALUCode), .sel(comparator_20_eq));  // open: in0
  Multiplexer #(.width(4)) multiplexer_12 (.in1(4'b0000), .out(ALUCode), .sel(comparator_2_eq));  // open: in0
  or or_5 (or_5_out, swSel, beqSel, bneSel, jSel);
  or or_6 (jalrSel, comparator_9_eq, comparator_11_eq);
  or or_7 (or_7_out, or_4_out, or_5_out);
  assign shiftAmount = {{27{Inst[10]}}, Inst[10:6]};  // Bit_Extender bit_extender_1
  not not_1 (regWriteE, or_7_out);
  or or_8 (immSel, jalrSel, lwSel, swSel, comparator_2_eq, jalSel);
  Multiplexer #(.width(5)) multiplexer_13 (
    .in0(multiplexer_2_out), .in1({5{1'b1}}), .out(multiplexer_13_out), .sel(jalSel));
  assign bit_extender_2_out = {{16{Inst[15]}}, Inst[15:0]};  // Bit_Extender bit_extender_2
  Multiplexer #(.width(5)) multiplexer_14 (.in0(multiplexer_13_out), .in1(5'b11010), .out(rd), .sel(comparator_9_eq));
  Multiplexer #(.width(32)) multiplexer_15 (
    .in0(bit_extender_2_out), .in1({{6{1'b0}}, Inst[25:0]}), .out(imm), .sel(or_2_out));

  assign rs = Inst[25:21];
  assign rt = Inst[20:16];

  // Notes on the sheet:
  //   addi
  //   lw
  //   sw
  //   beq
  //   bne
  //   j
  //   jal
  //   syscall
  //   jr
  //   jalr
  //   slt
  //   mflo
  //   mfhi
  //   sll
  //   srl
  //   mult
  //   div
  //   add
  //   sub
endmodule

module MemoryController (
  input  [25:0] AddressFromBus,
  input  WriteEnableFromBus,
  input  [31:0] DataFromBus,
  input  [31:0] DataFromMem,
  output [23:0] AddressToMem,
  output WriteEnableToMem,
  output WriteToBus,
  output [31:0] DataToMem,
  output [31:0] DataToBus
);

  wire comparator_1_lt;
  wire [25:0] shifter_1_out;

  Comparator #(.mode("unsigned"), .width(26)) comparator_1 (
    .a(AddressFromBus), .b(26'h3ffff00), .lt(comparator_1_lt));  // open: gt, eq
  and and_1 (WriteToBus, comparator_1_lt, ~WriteEnableFromBus);  // AND_Gate
  Shifter #(.shift("lr"), .width(26)) shifter_1 (.in(AddressFromBus), .\dist (5'b00010), .out(shifter_1_out));
  and and_2 (WriteEnableToMem, comparator_1_lt, WriteEnableFromBus);
  Bit_Extender #(.in_width(26), .out_width(24)) bit_extender_1 (.in(shifter_1_out), .out(AddressToMem));

  assign DataToBus = DataFromMem;
  assign DataToMem = DataFromBus;

  // Notes on the sheet:
  //   AddressFromBus: initial=0x3ffff00
endmodule

module KeyboardController (
  input  WriteEnableFromBus,
  input  [25:0] AddressFromBus,
  input  [31:0] DataFromBus,
  input  KeyboardStatus,
  input  [6:0] KeyboardData,
  output KeyboardRead,
  output WriteToBus,
  output [31:0] DataToBus
);

  wire and_1_out, and_2_out, comparator_1_eq, comparator_2_eq, not_1_out, or_1_out;
  wire [31:0] bit_extender_1_out, bit_extender_2_out, multiplexer_1_out;

  assign bit_extender_1_out = {{31{1'b0}}, KeyboardStatus};  // Bit_Extender bit_extender_1
  not not_1 (not_1_out, WriteEnableFromBus);
  Comparator #(.mode("unsigned"), .width(26)) comparator_1 (
    .a(AddressFromBus), .b(26'h3ffff10), .eq(comparator_1_eq));  // open: gt, lt
  Comparator #(.mode("unsigned"), .width(26)) comparator_2 (
    .a(AddressFromBus), .b(26'h3ffff14), .eq(comparator_2_eq));  // open: gt, lt
  Multiplexer #(.width(32)) multiplexer_1 (
    .in0(DataFromBus), .in1(bit_extender_1_out), .out(multiplexer_1_out), .sel(and_2_out));
  assign bit_extender_2_out = {{25{1'b0}}, KeyboardData};  // Bit_Extender bit_extender_2
  // Probe on multiplexer_1_out
  and and_1 (and_1_out, comparator_2_eq, not_1_out);
  Multiplexer #(.width(32)) multiplexer_2 (
    .in0(multiplexer_1_out), .in1(bit_extender_2_out), .out(DataToBus), .sel(and_1_out));
  and and_2 (and_2_out, not_1_out, comparator_1_eq);
  and and_3 (KeyboardRead, WriteEnableFromBus, comparator_1_eq);
  or or_1 (or_1_out, comparator_1_eq, comparator_2_eq);
  // Probe on not_1_out
  and and_4 (WriteToBus, or_1_out, not_1_out);
endmodule

module RGBController (
  input  [31:0] DataFromBus,
  input  WriteEnable,
  input  [25:0] AddressFromBus,
  output [7:0] RGBX,
  output [7:0] RGBY,
  output [23:0] RGBColor,
  output RGBWrite
);

  wire and_1_out, and_2_out, and_3_out, clock_1_out, clock_2_out, clock_3_out, comparator_1_eq,
       comparator_2_eq, comparator_3_eq, comparator_4_eq;
  wire [31:0] register_1_q, register_2_q, register_3_q;

  // Probe on WriteEnable
  // Probe on DataFromBus
  Comparator #(.mode("unsigned"), .width(26)) comparator_1 (
    .a(AddressFromBus), .b(26'h3ffff20), .eq(comparator_1_eq));  // open: gt, lt
  Comparator #(.mode("unsigned"), .width(26)) comparator_2 (
    .a(AddressFromBus), .b(26'h3ffff24), .eq(comparator_2_eq));  // open: gt, lt
  Comparator #(.mode("unsigned"), .width(26)) comparator_3 (
    .a(AddressFromBus), .b(26'h3ffff28), .eq(comparator_3_eq));  // open: gt, lt
  Comparator #(.mode("unsigned"), .width(26)) comparator_4 (
    .a(AddressFromBus), .b(26'h3ffff2c), .eq(comparator_4_eq));  // open: gt, lt
  and and_1 (and_1_out, comparator_1_eq, WriteEnable);
  and and_2 (and_2_out, comparator_2_eq, WriteEnable);
  and and_3 (and_3_out, comparator_3_eq, WriteEnable);
  and and_4 (RGBWrite, comparator_4_eq, WriteEnable);
  Register #(.width(32)) register_1 (
    .D(DataFromBus), .en(and_1_out), .clk(clock_1_out), .Q(register_1_q));  // open: clr
  Clock clock_1 (.out(clock_1_out));
  Register #(.width(32)) register_2 (
    .D(DataFromBus), .en(and_2_out), .clk(clock_2_out), .Q(register_2_q));  // open: clr
  Clock clock_2 (.out(clock_2_out));
  Register #(.width(32)) register_3 (
    .D(DataFromBus), .en(and_3_out), .clk(clock_3_out), .Q(register_3_q));  // open: clr
  Clock clock_3 (.out(clock_3_out));
  Bit_Extender #(.in_width(32), .out_width(8), .\type ("zero")) bit_extender_1 (.in(register_1_q), .out(RGBX));
  Bit_Extender #(.in_width(32), .out_width(8), .\type ("zero")) bit_extender_2 (.in(register_2_q), .out(RGBY));
  Bit_Extender #(.in_width(32), .out_width(24), .\type ("zero")) bit_extender_3 (.in(register_3_q), .out(RGBColor));
endmodule

module TerminalController (
  input  WriteEnableFromBus,
  input  [25:0] AddressFromBus,
  input  [31:0] DataFromBus,
  output WriteToTerminal,
  output [6:0] DataToTerminal
);

  wire comparator_1_eq;

  Comparator #(.mode("unsigned"), .width(26)) comparator_1 (
    .a(AddressFromBus), .b(26'h3ffff00), .eq(comparator_1_eq));  // open: gt, lt
  Bit_Extender #(.in_width(32), .out_width(7)) bit_extender_1 (.in(DataFromBus), .out(DataToTerminal));
  and and_1 (WriteToTerminal, WriteEnableFromBus, comparator_1_eq);
endmodule

module SoundController (
  input  [31:0] DataFromBus,
  input  [25:0] AddressFromBus,
  input  WriteEnable,
  output [13:0] Frequency,
  output SoundWriteEnable,
  output [6:0] Volume
);

  wire and_1_out, and_3_out, clock_1_out, clock_2_out, comparator_1_eq, comparator_2_eq, comparator_3_eq;
  wire [31:0] register_1_q, register_2_q;

  Comparator #(.mode("unsigned"), .width(26)) comparator_1 (
    .a(AddressFromBus), .b(26'h3ffff30), .eq(comparator_1_eq));  // open: gt, lt
  Comparator #(.mode("unsigned"), .width(26)) comparator_2 (
    .a(AddressFromBus), .b(26'h3ffff34), .eq(comparator_2_eq));  // open: gt, lt
  Comparator #(.mode("unsigned"), .width(26)) comparator_3 (
    .a(AddressFromBus), .b(26'h3ffff38), .eq(comparator_3_eq));  // open: gt, lt
  and and_1 (and_1_out, comparator_1_eq, WriteEnable);
  and and_2 (SoundWriteEnable, comparator_2_eq, WriteEnable);
  and and_3 (and_3_out, comparator_3_eq, WriteEnable);
  Register #(.width(32)) register_1 (
    .D(DataFromBus), .en(and_1_out), .clk(clock_1_out), .Q(register_1_q));  // open: clr
  Clock clock_1 (.out(clock_1_out));
  Register #(.width(32)) register_2 (
    .D(DataFromBus), .en(and_3_out), .clk(clock_2_out), .Q(register_2_q));  // open: clr
  Clock clock_2 (.out(clock_2_out));
  Bit_Extender #(.in_width(32), .out_width(14), .\type ("zero")) bit_extender_1 (.in(register_1_q), .out(Frequency));
  Bit_Extender #(.in_width(32), .out_width(7), .\type ("zero")) bit_extender_2 (.in(register_2_q), .out(Volume));
endmodule

module JoystickController (
  input  [3:0] X,
  input  [3:0] Y,
  input  [25:0] AddressFromBus,
  output [31:0] DataToBus,
  output JoyStickWriteEnable
);

  wire comparator_1_eq, comparator_2_eq;
  wire [3:0] multiplexer_1_out;

  Comparator #(.mode("unsigned"), .width(26)) comparator_1 (
    .a(AddressFromBus), .b(26'h3ffff3c), .eq(comparator_1_eq));  // open: gt, lt
  Comparator #(.mode("unsigned"), .width(26)) comparator_2 (
    .a(AddressFromBus), .b(26'h3ffff40), .eq(comparator_2_eq));  // open: gt, lt
  Multiplexer #(.width(4)) multiplexer_1 (.in0(X), .in1(Y), .out(multiplexer_1_out), .sel(comparator_2_eq));
  assign DataToBus = {{28{multiplexer_1_out[3]}}, multiplexer_1_out};  // Bit_Extender bit_extender_1
  or or_1 (JoyStickWriteEnable, comparator_1_eq, comparator_2_eq);
endmodule

module Computer (
);

  wire buzzer_1_p2, clock_1_out, clock_2_out, clock_3_out, cpu_1_buswriteenable,
       joystickcontroller_1_joystickwriteenable, keyboard_1_avail, keyboardcontroller_1_keyboardread,
       keyboardcontroller_1_writetobus, memorycontroller_1_writeenabletomem, memorycontroller_1_writetobus,
       rgb_video_1_p1, rgb_video_1_p2, soundcontroller_1_soundwriteenable,
       terminalcontroller_1_writetoterminal;
  wire [3:0] joystick_1_x, joystick_1_y;
  wire [6:0] keyboard_1_data, soundcontroller_1_volume, terminalcontroller_1_datatoterminal;
  wire [7:0] rgb_video_1_p3, rgb_video_1_p4;
  wire [13:0] soundcontroller_1_frequency;
  wire [23:0] memorycontroller_1_addresstomem, rgb_video_1_p5;
  wire [25:0] cpu_1_addresstobus;
  wire [31:0] controlled_buffer_1_out, cpu_1_datatobus, joystickcontroller_1_datatobus,
       keyboardcontroller_1_datatobus, memorycontroller_1_datatobus, memorycontroller_1_datatomem, ram_1_dout;

  RAM #(.addrWidth(24), .dataWidth(32), .enables("line")) ram_1 (
    .addr(memorycontroller_1_addresstomem), .we(memorycontroller_1_writeenabletomem), .clk(clock_1_out),
    .din(memorycontroller_1_datatomem), .dout(ram_1_dout));
  Clock clock_1 (.out(clock_1_out));
  // Probe on ram_1_dout
  KeyboardController keyboardcontroller_1 (
    .KeyboardStatus(keyboard_1_avail), .DataFromBus(controlled_buffer_1_out), .KeyboardData(keyboard_1_data),
    .WriteEnableFromBus(cpu_1_buswriteenable), .AddressFromBus(cpu_1_addresstobus),
    .KeyboardRead(keyboardcontroller_1_keyboardread), .DataToBus(keyboardcontroller_1_datatobus),
    .WriteToBus(keyboardcontroller_1_writetobus));
  MemoryController memorycontroller_1 (
    .DataFromMem(ram_1_dout), .WriteEnableFromBus(cpu_1_buswriteenable), .AddressFromBus(cpu_1_addresstobus),
    .DataFromBus(controlled_buffer_1_out), .AddressToMem(memorycontroller_1_addresstomem),
    .WriteEnableToMem(memorycontroller_1_writeenabletomem), .WriteToBus(memorycontroller_1_writetobus),
    .DataToMem(memorycontroller_1_datatomem), .DataToBus(memorycontroller_1_datatobus));
  CPU cpu_1 (
    .DataFromBus(controlled_buffer_1_out), .DataToBus(cpu_1_datatobus),
    .BusWriteEnable(cpu_1_buswriteenable), .AddressToBus(cpu_1_addresstobus));
  Clock clock_2 (.out(clock_2_out));
  Keyboard keyboard_1 (
    .clk(clock_2_out), .re(keyboardcontroller_1_keyboardread), .avail(keyboard_1_avail),
    .data(keyboard_1_data));  // open: clr
  // Probe on controlled_buffer_1_out
  assign controlled_buffer_1_out = memorycontroller_1_writetobus ? memorycontroller_1_datatobus : 32'bz;  // Controlled_Buffer controlled_buffer_1
  assign controlled_buffer_1_out = cpu_1_buswriteenable ? cpu_1_datatobus : 32'bz;  // Controlled_Buffer controlled_buffer_2
  // Probe on controlled_buffer_1_out
  assign controlled_buffer_1_out = keyboardcontroller_1_writetobus ? keyboardcontroller_1_datatobus : 32'bz;  // Controlled_Buffer controlled_buffer_3
  // Probe on cpu_1_buswriteenable
  // Probe on cpu_1_addresstobus
  // Probe on controlled_buffer_1_out
  Clock clock_3 (.out(clock_3_out));
  TTY tty_1 (
    .data(terminalcontroller_1_datatoterminal), .clk(clock_3_out), .we(terminalcontroller_1_writetoterminal));  // open: clr
  // RGB_Video #(.height(256), .scale(1), .width(256)) rgb_video_1: pin names not known; wires that end beside it: rgb_video_1_p1, rgb_video_1_p2, rgb_video_1_p3, rgb_video_1_p4, rgb_video_1_p5
  Clock clock_4 (.out(rgb_video_1_p1));
  Joystick joystick_1 (.x(joystick_1_x), .y(joystick_1_y));
  TerminalController terminalcontroller_1 (
    .WriteEnableFromBus(cpu_1_buswriteenable), .AddressFromBus(cpu_1_addresstobus),
    .DataFromBus(controlled_buffer_1_out), .WriteToTerminal(terminalcontroller_1_writetoterminal),
    .DataToTerminal(terminalcontroller_1_datatoterminal));
  RGBController rgbcontroller_1 (
    .DataFromBus(controlled_buffer_1_out), .WriteEnable(cpu_1_buswriteenable),
    .AddressFromBus(cpu_1_addresstobus), .RGBX(rgb_video_1_p3), .RGBY(rgb_video_1_p4),
    .RGBColor(rgb_video_1_p5), .RGBWrite(rgb_video_1_p2));
  JoystickController joystickcontroller_1 (
    .X(joystick_1_x), .Y(joystick_1_y), .AddressFromBus(cpu_1_addresstobus),
    .DataToBus(joystickcontroller_1_datatobus), .JoyStickWriteEnable(joystickcontroller_1_joystickwriteenable));
  SoundController soundcontroller_1 (
    .DataFromBus(controlled_buffer_1_out), .AddressFromBus(cpu_1_addresstobus),
    .WriteEnable(cpu_1_buswriteenable), .Frequency(soundcontroller_1_frequency),
    .SoundWriteEnable(soundcontroller_1_soundwriteenable), .Volume(soundcontroller_1_volume));
  assign controlled_buffer_1_out = joystickcontroller_1_joystickwriteenable ? joystickcontroller_1_datatobus : 32'bz;  // Controlled_Buffer controlled_buffer_4
  // Probe on controlled_buffer_1_out
  // Buzzer buzzer_1: pin names not known; wires that end beside it: soundcontroller_1_frequency, buzzer_1_p2, buzzer_1_p2, soundcontroller_1_volume, soundcontroller_1_frequency, soundcontroller_1_soundwriteenable, soundcontroller_1_volume

  // Notes on the sheet:
  //   Write_enable
  //   Address
  //   Data
endmodule
